// Logisim project extrastuff.circ as structural Verilog: 2 circuits, main circuit main
module main (
  input  Suboperation,
  input  [2:0] Op_Code,
  input  [15:0] A,
  input  [15:0] B,
  output Branch,
  output [15:0] Result
);

  wire comparator_1_eq, comparator_1_gt, comparator_1_lt, not_1_out;
  wire [15:0] adder_1_out, and_1_out, bit_extender_1_out, bit_extender_2_out, bit_extender_3_out,
       bit_extender_4_out, multiplexer_1_out, multiplexer_2_out, multiplexer_3_out, multiplexer_4_out,
       multiplexer_5_out, nor_1_out, shifter_1_out, shifter_2_out, subtractor_1_out;

  assign and_1_out = A & B;  // AND_Gate and_1, 16 bits wide
  assign nor_1_out = ~(A | B);  // NOR_Gate nor_1, 16 bits wide
  Adder #(.width(16)) adder_1 (.a(A), .b(B), .out(adder_1_out));  // open: cin, cout
  Subtractor #(.width(16)) subtractor_1 (.a(A), .b(B), .out(subtractor_1_out));  // open: bin, bout
  Shifter #(.width(16), .shift("lr")) shifter_1 (.in(A), .\dist (B[3:0]), .out(shifter_1_out));
  Shifter #(.width(16)) shifter_2 (.in(A), .\dist (B[3:0]), .out(shifter_2_out));
  Comparator #(.width(16)) comparator_1 (
    .a(A), .b(B), .gt(comparator_1_gt), .eq(comparator_1_eq), .lt(comparator_1_lt));
  Multiplexer #(.width(16)) multiplexer_1 (
    .in0(and_1_out), .in1(nor_1_out), .out(multiplexer_1_out), .sel(Suboperation));  // open: en
  Multiplexer #(.width(16)) multiplexer_2 (
    .in0(adder_1_out), .in1(subtractor_1_out), .out(multiplexer_2_out), .sel(Suboperation));  // open: en
  Multiplexer #(.width(16)) multiplexer_3 (
    .in0(shifter_1_out), .in1(shifter_2_out), .out(multiplexer_3_out), .sel(Suboperation));  // open: en
  not not_1 (not_1_out, comparator_1_eq);
  assign bit_extender_1_out = {{15{1'b0}}, not_1_out};  // Bit_Extender bit_extender_1
  assign bit_extender_2_out = {{15{1'b0}}, comparator_1_eq};  // Bit_Extender bit_extender_2
  assign bit_extender_3_out = {{15{1'b0}}, comparator_1_gt};  // Bit_Extender bit_extender_3
  assign bit_extender_4_out = {{15{1'b0}}, comparator_1_lt};  // Bit_Extender bit_extender_4
  Multiplexer #(.width(16)) multiplexer_4 (
    .in0(bit_extender_1_out), .in1(bit_extender_2_out), .out(multiplexer_4_out), .sel(Suboperation));  // open: en
  Multiplexer #(.width(16)) multiplexer_5 (
    .in0(bit_extender_3_out), .in1(bit_extender_4_out), .out(multiplexer_5_out), .sel(Suboperation));  // open: en
  Multiplexer #(.select(3), .width(16)) multiplexer_6 (
    .in0(multiplexer_1_out), .in1(adder_1_out), .in2(multiplexer_2_out), .in3(multiplexer_3_out),
    .in4(multiplexer_4_out), .in5(multiplexer_5_out), .in6(multiplexer_5_out), .in7(multiplexer_5_out),
    .out(Result), .sel(Op_Code));  // open: en
  or or_1 (Branch, Result[0], Result[1], Result[2], Result[3], Result[4], Result[5], Result[6], Result[7], Result[8], Result[9], Result[10], Result[11], Result[12], Result[13], Result[14], Result[15]);
endmodule

module \output  (
  input  [15:0] Output,
  input  EN,
  input  CLK,
  input  CLR,
  output [3:0] Out_0,
  output [3:0] Out_1,
  output [3:0] Out_2,
  output [3:0] Out_3
);

  Register #(.width(16)) register_1 (.D(Output), .en(EN), .Q({Out_3, Out_2, Out_1, Out_0}), .clk(CLK), .clr(CLR));
endmodule
