// Logisim project COEMIPS.circ as structural Verilog: 10 circuits, main circuit main
module main (
);

  wire branch_1_conditionmet, button_1_out, button_2_out, clock_1_out, control_signals_1_alusrc,
       control_signals_1_halt, control_signals_1_memread, control_signals_1_memtoreg,
       control_signals_1_memwrite, control_signals_1_put, control_signals_1_regwrite,
       control_signals_1_shift, control_signals_1_shiftright, control_signals_1_shiftsrc, jump_1_jr,
       jump_1_jumpandlink, jump_1_jumpimmediate;
  wire [1:0] control_signals_1_aluop0;
  wire [3:0] multiplexer_3_out, put_1_led0, put_1_led1, put_1_led2, put_1_led3;
  wire [7:0] multiplexer_1_out, multiplexer_4_out, multiplexer_6_out, pc_1_pc___1, pc_1_pc_out;
  wire [15:0] alu_1_result, extend_1_data_out, extend_2_data_out, multiplexer_2_out, multiplexer_5_out,
       multiplexer_7_out, multiplexer_8_out, ram_1_data, registers_1_read_1, registers_1_read_2, rom_1_data,
       shift_1_shift_output;

  LED HALT (.in(control_signals_1_halt));
  Clock clock_1 (.out(clock_1_out));
  PC pc_1 (
    .PC(multiplexer_1_out), .Halt(control_signals_1_halt), .CK(clock_1_out), .Reset(button_1_out),
    .PC_Out(pc_1_pc_out), .PC___1(pc_1_pc___1));
  Button button_1 (.out(button_1_out));
  ROM #(.dataWidth(16)) rom_1 (.addr(pc_1_pc_out), .data(rom_1_data));  // open: sel
  Jump jump_1 (
    .OpCode3(rom_1_data[15]), .OpCode2(rom_1_data[14]), .OpCode1(rom_1_data[13]), .OpCode0(rom_1_data[12]),
    .SubOp(rom_1_data[0]), .JR(jump_1_jr), .JumpImmediate(jump_1_jumpimmediate),
    .JumpAndLink(jump_1_jumpandlink));
  Control_Signals control_signals_1 (
    .OpCode3(rom_1_data[15]), .OpCode2(rom_1_data[14]), .OpCode1(rom_1_data[13]), .OpCode0(rom_1_data[12]),
    .SubOp(rom_1_data[0]), .MemRead(control_signals_1_memread), .MemWrite(control_signals_1_memwrite),
    .MemtoReg(control_signals_1_memtoreg), .RegWrite(control_signals_1_regwrite),
    .ALUSrc(control_signals_1_alusrc), .ALUOp1(control_signals_1_aluop0[1]),
    .ALUOp0(control_signals_1_aluop0[0]), .Put(control_signals_1_put), .Halt(control_signals_1_halt),
    .Shift(control_signals_1_shift), .ShiftSrc(control_signals_1_shiftsrc),
    .ShiftRight(control_signals_1_shiftright));
  Multiplexer #(.width(8), .enable("false")) multiplexer_1 (
    .in0(multiplexer_6_out), .in1(multiplexer_4_out), .out(multiplexer_1_out), .sel(jump_1_jr));
  Registers registers_1 (
    .Read_Register_1(rom_1_data[11:9]), .Write_Enable(control_signals_1_regwrite),
    .Write_Register(rom_1_data[11:9]), .Write_Data(multiplexer_8_out), .Read_Register_2(rom_1_data[8:6]),
    .Reset(button_1_out), .Clock(clock_1_out), .Read_1(registers_1_read_1), .Read_2(registers_1_read_2));
  Extend extend_1 (.Data_In(rom_1_data[8:1]), .Unsigned(rom_1_data[0]), .Data_Out(extend_1_data_out));
  Branch branch_1 (
    .OpCode(rom_1_data[15:12]), .Data(registers_1_read_1), .ConditionMet(branch_1_conditionmet));  // open: IsBranch
  Multiplexer #(.width(16), .enable("false")) multiplexer_2 (
    .in0(registers_1_read_2), .in1(extend_1_data_out), .out(multiplexer_2_out), .sel(control_signals_1_alusrc));
  ALU alu_1 (
    .A(registers_1_read_1), .B(multiplexer_2_out), .Operation(control_signals_1_aluop0), .Result(alu_1_result));  // open: Zero
  Shift shift_1 (
    .SR(control_signals_1_shiftright), .Data_In(registers_1_read_1), .Shift_Distance(multiplexer_3_out),
    .Shift_Output(shift_1_shift_output));
  Multiplexer #(.width(4), .enable("false")) multiplexer_3 (
    .in0(registers_1_read_2[3:0]), .in1(rom_1_data[4:1]), .out(multiplexer_3_out),
    .sel(control_signals_1_shiftsrc));
  Put put_1 (
    .D(registers_1_read_1), .Put_Enable(control_signals_1_put), .CK(clock_1_out), .Reset(button_1_out),
    .LED0(put_1_led0), .LED1(put_1_led1), .LED2(put_1_led2), .LED3(put_1_led3));
  Multiplexer #(.width(8), .enable("false")) multiplexer_4 (
    .in0(registers_1_read_1[7:0]), .in1(rom_1_data[8:1]), .out(multiplexer_4_out), .sel(jump_1_jumpimmediate));
  Hex_Digit_Display hex_digit_display_1 (.value(put_1_led2));  // open: dp
  Hex_Digit_Display hex_digit_display_2 (.value(put_1_led3));  // open: dp
  RAM #(.dataWidth(16), .bus("separate")) ram_1 (
    .addr(registers_1_read_2[7:0]), .din(registers_1_read_1), .data(ram_1_data),
    .str(control_signals_1_memwrite), .clk(clock_1_out), .ld(control_signals_1_memread), .clr(button_2_out));  // open: sel
  Button button_2 (.out(button_2_out));
  Hex_Digit_Display hex_digit_display_3 (.value(put_1_led0));  // open: dp
  Hex_Digit_Display hex_digit_display_4 (.value(put_1_led1));  // open: dp
  Multiplexer #(.width(16), .enable("false")) multiplexer_5 (
    .in0(alu_1_result), .in1(ram_1_data), .out(multiplexer_5_out), .sel(control_signals_1_memtoreg));
  Multiplexer #(.width(8), .enable("false")) multiplexer_6 (
    .in0(pc_1_pc___1), .in1(rom_1_data[8:1]), .out(multiplexer_6_out), .sel(branch_1_conditionmet));
  Multiplexer #(.width(16), .enable("false")) multiplexer_7 (
    .in0(multiplexer_5_out), .in1(shift_1_shift_output), .out(multiplexer_7_out),
    .sel(control_signals_1_shift));
  Multiplexer #(.width(16), .enable("false")) multiplexer_8 (
    .in0(multiplexer_7_out), .in1(extend_2_data_out), .out(multiplexer_8_out), .sel(jump_1_jumpandlink));
  Extend extend_2 (.Data_In(pc_1_pc___1), .Unsigned(1'b1), .Data_Out(extend_2_data_out));

  // Notes on the sheet:
  //   contents of rom_1 (hex, n*v repeats v):
  //   6 f000 4 f000 7000
  //   Avery Peiffer
  //   aep65@pitt.edu
endmodule

module ALU (
  input  [1:0] Operation,
  input  [15:0] A,
  input  [15:0] B,
  output [15:0] Result,
  output Zero
);

  wire [15:0] adder_1_out, and_1_out, multiplexer_1_out, nor_1_out, not_1_out;

  assign not_1_out = ~B;  // NOT_Gate not_1, 16 bits wide
  Multiplexer #(.select(2), .width(16), .enable("false")) multiplexer_1 (
    .in2(B), .in3(not_1_out), .out(multiplexer_1_out), .sel(Operation));  // open: in0, in1
  assign and_1_out = A & B;  // AND_Gate and_1, 16 bits wide
  assign nor_1_out = ~(A | B);  // NOR_Gate nor_1, 16 bits wide
  Adder #(.width(16)) adder_1 (.a(A), .b(multiplexer_1_out), .out(adder_1_out), .cin(Operation[0]));  // open: cout
  Multiplexer #(.select(2), .width(16), .enable("false")) multiplexer_2 (
    .in0(and_1_out), .in1(nor_1_out), .in2(adder_1_out), .in3(adder_1_out), .out(Result), .sel(Operation));
  nor nor_2 (Zero, Result[15], Result[14], Result[13], Result[12], Result[11], Result[10], Result[9], Result[8], Result[7], Result[6], Result[5], Result[4], Result[3], Result[2], Result[1], Result[0]);
endmodule

module Branch (
  input  [3:0] OpCode,
  input  [15:0] Data,
  output IsBranch,
  output ConditionMet
);

  wire comparator_1_eq, comparator_1_gt, comparator_1_lt, multiplexer_1_out, not_1_out;

  Comparator #(.width(16)) comparator_1 (
    .a(Data), .b({16{1'b0}}), .gt(comparator_1_gt), .eq(comparator_1_eq), .lt(comparator_1_lt));
  not not_1 (not_1_out, comparator_1_gt);
  and and_1 (IsBranch, OpCode[3], ~OpCode[2]);  // AND_Gate
  Multiplexer #(.select(2), .enable("false")) multiplexer_1 (
    .in0(comparator_1_eq), .in1(comparator_1_gt), .in2(comparator_1_lt), .in3(not_1_out),
    .out(multiplexer_1_out), .sel(OpCode[1:0]));
  and and_2 (ConditionMet, IsBranch, multiplexer_1_out);
endmodule

module Control_Signals (
  input  OpCode3,
  input  OpCode2,
  input  OpCode1,
  input  OpCode0,
  input  SubOp,
  output MemRead,
  output MemWrite,
  output MemtoReg,
  output RegWrite,
  output ALUSrc,
  output ALUOp1,
  output ALUOp0,
  output Put,
  output Halt,
  output Shift,
  output ShiftSrc,
  output ShiftRight
);

  wire and_4_out, and_5_out, and_7_out, and_8_out, nand_1_out, not_1_out, not_2_out, not_3_out, not_4_out,
       not_5_out, not_6_out, not_7_out, not_8_out, not_9_out, not_10_out, not_11_out, not_12_out, not_13_out,
       not_14_out, not_16_out, not_17_out, not_18_out, not_19_out, not_20_out, not_21_out, xor_1_out;

  not not_1 (not_1_out, OpCode3);
  not not_2 (not_2_out, OpCode1);
  not not_3 (not_3_out, OpCode0);
  not not_4 (not_4_out, OpCode3);
  not not_5 (not_5_out, OpCode1);
  not not_6 (not_6_out, OpCode0);
  not not_7 (not_7_out, SubOp);
  not not_8 (not_8_out, OpCode3);
  not not_9 (not_9_out, OpCode2);
  not not_10 (not_10_out, OpCode3);
  nand nand_1 (nand_1_out, OpCode1, OpCode0);
  not not_11 (not_11_out, OpCode3);
  not not_12 (not_12_out, OpCode2);
  not not_13 (not_13_out, OpCode1);
  not not_14 (not_14_out, OpCode0);
  not not_15 (ALUOp1, OpCode1);
  not not_16 (not_16_out, OpCode0);
  not not_17 (not_17_out, SubOp);
  and and_1 (Put, OpCode3, OpCode2, OpCode1, OpCode0);
  not not_18 (not_18_out, OpCode3);
  not not_19 (not_19_out, OpCode3);
  xor xor_1 (xor_1_out, OpCode1, OpCode0);
  not not_20 (not_20_out, OpCode3);
  not not_21 (not_21_out, OpCode1);
  not not_22 (ShiftRight, SubOp);
  and and_2 (MemWrite, not_1_out, OpCode2, not_2_out, not_3_out, SubOp);
  and and_3 (MemtoReg, not_4_out, OpCode2, not_5_out, not_6_out, not_7_out);
  and and_4 (and_4_out, not_8_out, not_9_out);
  and and_5 (and_5_out, not_10_out, OpCode2, nand_1_out);
  and and_6 (ALUSrc, not_11_out, not_12_out, not_13_out, not_14_out);
  and and_7 (and_7_out, not_16_out, SubOp);
  and and_8 (and_8_out, OpCode1, not_17_out);
  and and_9 (Halt, not_18_out, OpCode2, OpCode1, OpCode0);
  and and_10 (Shift, not_19_out, OpCode2, xor_1_out);
  and and_11 (ShiftSrc, not_20_out, OpCode2, not_21_out, OpCode0);
  or or_1 (RegWrite, and_4_out, and_5_out);
  or or_2 (ALUOp0, and_7_out, and_8_out);

  assign MemRead = 1'b1;
endmodule

module Extend (
  input  [7:0] Data_In,
  input  Unsigned,
  output [15:0] Data_Out
);

  wire [15:0] bit_extender_1_out, bit_extender_2_out;

  assign bit_extender_1_out = {{8{Data_In[7]}}, Data_In};  // Bit_Extender bit_extender_1
  assign bit_extender_2_out = {{8{1'b0}}, Data_In};  // Bit_Extender bit_extender_2
  Multiplexer #(.width(16), .enable("false")) multiplexer_1 (
    .in0(bit_extender_1_out), .in1(bit_extender_2_out), .out(Data_Out), .sel(Unsigned));
endmodule

module Jump (
  input  OpCode3,
  input  OpCode2,
  input  OpCode1,
  input  OpCode0,
  input  SubOp,
  output JR,
  output JumpImmediate,
  output JumpAndLink
);

  wire not_1_out, not_2_out, not_3_out, not_4_out, not_5_out;

  not not_1 (not_1_out, OpCode1);
  not not_2 (not_2_out, SubOp);
  not not_3 (not_3_out, OpCode0);
  not not_4 (not_4_out, OpCode1);
  not not_5 (not_5_out, OpCode0);
  and and_1 (JR, OpCode3, OpCode2, not_1_out, OpCode0, not_2_out);
  and and_2 (JumpImmediate, OpCode3, OpCode2, OpCode1, not_3_out);
  and and_3 (JumpAndLink, OpCode3, OpCode2, not_4_out, not_5_out);
endmodule

module PC (
  input  [7:0] PC,
  input  Halt,
  input  CK,
  input  Reset,
  output [7:0] PC_Out,
  output [7:0] PC___1
);

  wire not_1_out;

  not not_1 (not_1_out, Halt);
  Register register_1 (.D(PC), .en(not_1_out), .Q(PC_Out), .clk(CK), .clr(Reset));
  Adder adder_1 (.a(PC_Out), .b(8'h1), .out(PC___1));  // open: cin, cout
endmodule

module Put (
  input  [15:0] D,
  input  Put_Enable,
  input  CK,
  input  Reset,
  output [3:0] LED0,
  output [3:0] LED1,
  output [3:0] LED2,
  output [3:0] LED3
);

  Register #(.width(16)) register_1 (.D(D), .en(Put_Enable), .Q({LED3, LED2, LED1, LED0}), .clk(CK), .clr(Reset));
endmodule

module Registers (
  input  [2:0] Read_Register_1,
  input  Write_Enable,
  input  [2:0] Write_Register,
  input  [15:0] Write_Data,
  input  Reset,
  input  Clock,
  input  [2:0] Read_Register_2,
  output [15:0] Read_1,
  output [15:0] Read_2
);

  wire demultiplexer_1_out0, demultiplexer_1_out1, demultiplexer_1_out2, demultiplexer_1_out3,
       demultiplexer_1_out4, demultiplexer_1_out5, demultiplexer_1_out6, demultiplexer_1_out7;
  wire [15:0] demultiplexer_2_out0, demultiplexer_2_out1, demultiplexer_2_out2, demultiplexer_2_out3,
       demultiplexer_2_out4, demultiplexer_2_out5, demultiplexer_2_out6, demultiplexer_2_out7, R0_q, R1_q,
       R2_q, R3_q, R4_q, R5_q, R6_q, R7_q;

  Demultiplexer #(.select(3)) demultiplexer_1 (
    .out0(demultiplexer_1_out0), .out1(demultiplexer_1_out1), .out2(demultiplexer_1_out2),
    .out3(demultiplexer_1_out3), .out4(demultiplexer_1_out4), .out5(demultiplexer_1_out5),
    .out6(demultiplexer_1_out6), .out7(demultiplexer_1_out7), .in(1'b1), .sel(Write_Register),
    .en(Write_Enable));
  Demultiplexer #(.select(3), .width(16), .enable("false")) demultiplexer_2 (
    .out0(demultiplexer_2_out0), .out1(demultiplexer_2_out1), .out2(demultiplexer_2_out2),
    .out3(demultiplexer_2_out3), .out4(demultiplexer_2_out4), .out5(demultiplexer_2_out5),
    .out6(demultiplexer_2_out6), .out7(demultiplexer_2_out7), .in(Write_Data), .sel(Write_Register));
  Register #(.width(16)) R0 (.D(demultiplexer_2_out0), .en(demultiplexer_1_out0), .Q(R0_q), .clk(Clock), .clr(Reset));
  Register #(.width(16)) R1 (.D(demultiplexer_2_out1), .en(demultiplexer_1_out1), .Q(R1_q), .clk(Clock), .clr(Reset));
  Register #(.width(16)) R2 (.D(demultiplexer_2_out2), .en(demultiplexer_1_out2), .Q(R2_q), .clk(Clock), .clr(Reset));
  Register #(.width(16)) R3 (.D(demultiplexer_2_out3), .en(demultiplexer_1_out3), .Q(R3_q), .clk(Clock), .clr(Reset));
  Register #(.width(16)) R4 (.D(demultiplexer_2_out4), .en(demultiplexer_1_out4), .Q(R4_q), .clk(Clock), .clr(Reset));
  Register #(.width(16)) R5 (.D(demultiplexer_2_out5), .en(demultiplexer_1_out5), .Q(R5_q), .clk(Clock), .clr(Reset));
  Register #(.width(16)) R6 (.D(demultiplexer_2_out6), .en(demultiplexer_1_out6), .Q(R6_q), .clk(Clock), .clr(Reset));
  Register #(.width(16)) R7 (.D(demultiplexer_2_out7), .en(demultiplexer_1_out7), .Q(R7_q), .clk(Clock), .clr(Reset));
  Multiplexer #(.select(3), .width(16), .enable("false")) multiplexer_1 (
    .in0(R0_q), .in1(R1_q), .in2(R2_q), .in3(R3_q), .in4(R4_q), .in5(R5_q), .in6(R6_q), .in7(R7_q),
    .out(Read_1), .sel(Read_Register_1));
  Multiplexer #(.select(3), .width(16), .enable("false")) multiplexer_2 (
    .in0(R0_q), .in1(R1_q), .in2(R2_q), .in3(R3_q), .in4(R4_q), .in5(R5_q), .in6(R6_q), .in7(R7_q),
    .out(Read_2), .sel(Read_Register_2));
endmodule

module Shift (
  input  SR,
  input  [15:0] Data_In,
  input  [3:0] Shift_Distance,
  output [15:0] Shift_Output
);

  wire [15:0] shifter_1_out, shifter_2_out;

  Shifter #(.width(16), .shift("lr")) shifter_1 (.in(Data_In), .\dist (Shift_Distance), .out(shifter_1_out));
  Shifter #(.width(16)) shifter_2 (.in(Data_In), .\dist (Shift_Distance), .out(shifter_2_out));
  Multiplexer #(.width(16), .enable("false")) multiplexer_1 (
    .in0(shifter_2_out), .in1(shifter_1_out), .out(Shift_Output), .sel(SR));
endmodule
