// Logisim project Lab11_aep65.circ as structural Verilog: 1 circuit, main circuit main
module main (
  input  Input,
  output Output
);

  wire and_1_out, and_2_out, and_3_out, and_4_out, and_5_out, and_6_out, and_7_out, and_8_out, clock_1_out,
       D0_q, D0_qn, D1_q, D1_qn, D2_q, D2_qn, not_1_out, or_1_out, or_2_out, or_3_out;

  Clock clock_1 (.out(clock_1_out));
  D_Flip_Flop D0 (.clk(clock_1_out), .D(or_1_out), .Q(D0_q), .Qn(D0_qn));  // open: preset, en, reset
  D_Flip_Flop D1 (.clk(clock_1_out), .D(or_2_out), .Q(D1_q), .Qn(D1_qn));  // open: preset, en, reset
  D_Flip_Flop D2 (.clk(clock_1_out), .D(or_3_out), .Q(D2_q), .Qn(D2_qn));  // open: preset, en, reset
  and and_1 (and_1_out, Input, D0_qn);
  and and_2 (and_2_out, D0_qn, D2_q);
  and and_3 (and_3_out, Input, D2_q);
  and and_4 (and_4_out, Input, D1_qn, D2_qn);
  not not_1 (not_1_out, Input);
  or or_1 (or_1_out, and_1_out, and_2_out, and_3_out, and_4_out);
  and and_5 (and_5_out, D1_q, D0_qn, Input);
  and and_6 (and_6_out, not_1_out, D2_qn, D0_q);
  and and_7 (and_7_out, not_1_out, D2_q, D0_qn);
  and and_8 (and_8_out, Input, D1_q, D0_q);
  or or_2 (or_2_out, and_5_out, and_6_out);
  or or_3 (or_3_out, and_7_out, and_8_out);
  and and_9 (Output, Input, D0_q, ~D1_q, D2_q);  // AND_Gate
endmodule
