// Logisim project Lab9_aep65.circ as structural Verilog: 3 circuits, main circuit main
module main (
  input  [1:0] Operation,
  input  Ainvert,
  input  Bnegate,
  input  [7:0] A,
  input  [7:0] B,
  output [7:0] Result,
  output Zero,
  output Overflow
);

  _8_bit_ALU u_8_bit_alu_1 (
    .A(A), .B(B), .Ainvert(Bnegate), .Bnegate(Ainvert), .Operation(Operation), .Result(Result), .Zero(Zero),
    .Overflow(Overflow));
endmodule

module _1_bit_ALU (
  input  Carryin,
  input  A,
  input  AInvert,
  input  B,
  input  BInvert,
  input  Less,
  input  [1:0] Operation,
  output Result,
  output Set,
  output CarryOut
);

  wire and_1_out, multiplexer_1_out, multiplexer_2_out, not_1_out, not_2_out, or_1_out;

  not not_1 (not_1_out, A);
  not not_2 (not_2_out, B);
  Multiplexer multiplexer_1 (.in0(A), .in1(not_1_out), .out(multiplexer_1_out), .sel(AInvert));  // open: en
  Multiplexer multiplexer_2 (.in0(B), .in1(not_2_out), .out(multiplexer_2_out), .sel(BInvert));  // open: en
  and and_1 (and_1_out, multiplexer_1_out, multiplexer_2_out);
  or or_1 (or_1_out, multiplexer_1_out, multiplexer_2_out);
  Adder #(.width(1)) adder_1 (.a(multiplexer_1_out), .b(multiplexer_2_out), .out(Set), .cin(Carryin), .cout(CarryOut));
  Multiplexer #(.select(2)) multiplexer_3 (
    .in0(and_1_out), .in1(or_1_out), .in2(Set), .in3(Less), .out(Result), .sel(Operation));  // open: en
endmodule

module _8_bit_ALU (
  input  Ainvert,
  input  Bnegate,
  input  [1:0] Operation,
  input  [7:0] A,
  input  [7:0] B,
  output [7:0] Result,
  output Zero,
  output Overflow
);

  wire n1_bit_alu_1_carryout, n1_bit_alu_2_carryout, n1_bit_alu_3_carryout, n1_bit_alu_4_carryout,
       n1_bit_alu_5_carryout, n1_bit_alu_6_carryout, n1_bit_alu_7_carryout, n1_bit_alu_8_carryout,
       n1_bit_alu_8_set, or_1_out, xor_1_out;

  xor xor_1 (xor_1_out, n1_bit_alu_8_set, Overflow);
  _1_bit_ALU u_1_bit_alu_1 (
    .Carryin(Bnegate), .A(A[0]), .AInvert(Ainvert), .B(B[0]), .BInvert(Bnegate), .Less(xor_1_out),
    .Operation(Operation), .Result(Result[0]), .CarryOut(n1_bit_alu_1_carryout));  // open: Set
  _1_bit_ALU u_1_bit_alu_2 (
    .Carryin(n1_bit_alu_1_carryout), .A(A[1]), .AInvert(Ainvert), .B(B[1]), .BInvert(Bnegate), .Less(1'b0),
    .Operation(Operation), .Result(Result[1]), .CarryOut(n1_bit_alu_2_carryout));  // open: Set
  _1_bit_ALU u_1_bit_alu_3 (
    .Carryin(n1_bit_alu_2_carryout), .A(A[2]), .AInvert(Ainvert), .B(B[2]), .BInvert(Bnegate), .Less(1'b0),
    .Operation(Operation), .Result(Result[2]), .CarryOut(n1_bit_alu_3_carryout));  // open: Set
  _1_bit_ALU u_1_bit_alu_4 (
    .Carryin(n1_bit_alu_3_carryout), .A(A[3]), .AInvert(Ainvert), .B(B[3]), .BInvert(Bnegate), .Less(1'b0),
    .Operation(Operation), .Result(Result[3]), .CarryOut(n1_bit_alu_4_carryout));  // open: Set
  _1_bit_ALU u_1_bit_alu_5 (
    .Carryin(n1_bit_alu_4_carryout), .A(A[4]), .AInvert(Ainvert), .B(B[4]), .BInvert(Bnegate), .Less(1'b0),
    .Operation(Operation), .Result(Result[4]), .CarryOut(n1_bit_alu_5_carryout));  // open: Set
  _1_bit_ALU u_1_bit_alu_6 (
    .Carryin(n1_bit_alu_5_carryout), .A(A[5]), .AInvert(Ainvert), .B(B[5]), .BInvert(Bnegate), .Less(1'b0),
    .Operation(Operation), .Result(Result[5]), .CarryOut(n1_bit_alu_6_carryout));  // open: Set
  _1_bit_ALU u_1_bit_alu_7 (
    .Carryin(n1_bit_alu_6_carryout), .A(A[6]), .AInvert(Ainvert), .B(B[6]), .BInvert(Bnegate), .Less(1'b0),
    .Operation(Operation), .Result(Result[6]), .CarryOut(n1_bit_alu_7_carryout));  // open: Set
  _1_bit_ALU u_1_bit_alu_8 (
    .Carryin(n1_bit_alu_7_carryout), .A(A[7]), .AInvert(Ainvert), .B(B[7]), .BInvert(Bnegate), .Less(1'b0),
    .Operation(Operation), .Result(Result[7]), .Set(n1_bit_alu_8_set), .CarryOut(n1_bit_alu_8_carryout));
  or or_1 (or_1_out, Result[0], Result[1], Result[2], Result[7]);
  xor xor_2 (Overflow, n1_bit_alu_7_carryout, n1_bit_alu_8_carryout);
  not not_1 (Zero, or_1_out);
endmodule
