// Logisim project aep65_Lab10Part2.circ as structural Verilog: 1 circuit, main circuit main
module main (
  input  [7:0] Data
);

  wire and_1_out, Clock_out, counter_1_carry, d_ff_1_q, not_1_out, not_2_out, or_1_out, Reset_out;
  wire [7:0] counter_1_q, ram_1_data;

  Clock Clock (.out(Clock_out));
  and and_1 (and_1_out, Clock_out, not_1_out);
  Button Reset (.out(Reset_out));
  Counter counter_1 (
    .count(Clock_out), .Q(counter_1_q), .carry(counter_1_carry), .clk(and_1_out), .clr(Reset_out));  // open: load, D
  not not_1 (not_1_out, counter_1_carry);
  D_Flip_Flop d_ff_1 (.clk(Clock_out), .D(not_1_out), .Q(d_ff_1_q));  // open: Qn, preset, en, reset
  RAM ram_1 (.addr(counter_1_q), .data(ram_1_data), .clk(Clock_out), .ld(not_2_out));  // open: sel, clr
  not not_2 (not_2_out, or_1_out);
  assign ram_1_data = or_1_out ? Data : 8'bz;  // Controlled_Buffer controlled_buffer_1
  or or_1 (or_1_out, not_1_out, d_ff_1_q);
endmodule
