// Logisim project aep65_lab8_part2.circ as structural Verilog: 2 circuits, main circuit main
module main (
);

  wire button_1_out, button_2_out, button_3_out, button_4_out, button_5_out, button_6_out, clock_1_out,
       timeralert_1_alert, timeralert_1_timer_expired, timeralert_2_alert, timeralert_2_timer_expired,
       timeralert_3_alert, timeralert_3_timer_expired, timeralert_4_alert, timeralert_4_timer_expired,
       timeralert_5_alert, timeralert_5_timer_expired, timeralert_6_alert, timeralert_6_timer_expired;

  Button button_1 (.out(button_1_out));
  Button button_2 (.out(button_2_out));
  Button button_3 (.out(button_3_out));
  Button button_4 (.out(button_4_out));
  Button button_5 (.out(button_5_out));
  Button button_6 (.out(button_6_out));
  Clock clock_1 (.out(clock_1_out));
  TimerAlert timeralert_1 (
    .Reset(button_1_out), .Clock_Input(clock_1_out), .Timer_Expired(timeralert_1_timer_expired),
    .Alert(timeralert_1_alert));
  TimerAlert timeralert_2 (
    .Reset(button_2_out), .Clock_Input(clock_1_out), .Timer_Expired(timeralert_2_timer_expired),
    .Alert(timeralert_2_alert));
  TimerAlert timeralert_3 (
    .Reset(button_3_out), .Clock_Input(clock_1_out), .Timer_Expired(timeralert_3_timer_expired),
    .Alert(timeralert_3_alert));
  TimerAlert timeralert_4 (
    .Reset(button_4_out), .Clock_Input(clock_1_out), .Timer_Expired(timeralert_4_timer_expired),
    .Alert(timeralert_4_alert));
  TimerAlert timeralert_5 (
    .Reset(button_5_out), .Clock_Input(clock_1_out), .Timer_Expired(timeralert_5_timer_expired),
    .Alert(timeralert_5_alert));
  TimerAlert timeralert_6 (
    .Reset(button_6_out), .Clock_Input(clock_1_out), .Timer_Expired(timeralert_6_timer_expired),
    .Alert(timeralert_6_alert));
  LED led_1 (.in(timeralert_1_timer_expired));
  LED led_2 (.in(timeralert_1_alert));
  LED led_3 (.in(timeralert_2_timer_expired));
  LED led_4 (.in(timeralert_2_alert));
  LED led_5 (.in(timeralert_3_timer_expired));
  LED led_6 (.in(timeralert_3_alert));
  LED led_7 (.in(timeralert_4_timer_expired));
  LED led_8 (.in(timeralert_4_alert));
  LED led_9 (.in(timeralert_5_timer_expired));
  LED led_10 (.in(timeralert_5_alert));
  LED led_11 (.in(timeralert_6_timer_expired));
  LED led_12 (.in(timeralert_6_alert));

  // Notes on the sheet:
  //   Reset_Button
  //   Reset_Button
  //   Reset_Button
  //   Reset_Button
  //   Reset_Button
  //   Reset_Button
  //   Clock
endmodule

module TimerAlert (
  input  Reset,
  input  Clock_Input,
  output Timer_Expired,
  output Alert
);

  wire and_1_out, and_2_out, and_3_out, and_4_out, and_5_out, and_6_out, and_7_out, and_8_out;
  wire [8:0] counter_1_q;

  Counter #(.width(10), .max('h3ff), .ongoal("stay")) counter_1 (
    .Q({Alert, counter_1_q}), .clk(Clock_Input), .clr(Reset));  // open: load, D, count, carry
  and and_1 (and_1_out, counter_1_q[0], counter_1_q[1]);
  and and_2 (and_2_out, counter_1_q[2], counter_1_q[3]);
  and and_3 (and_3_out, counter_1_q[6], counter_1_q[7]);
  and and_4 (and_4_out, counter_1_q[8], Alert);
  and and_5 (and_5_out, and_1_out, and_2_out);
  and and_6 (and_6_out, counter_1_q[4], counter_1_q[5]);
  and and_7 (and_7_out, and_3_out, and_4_out);
  and and_8 (and_8_out, and_5_out, and_6_out);
  and and_9 (Timer_Expired, and_8_out, and_7_out);
endmodule
