// Logisim project coemips_aep65.circ as structural Verilog
module main (
);

  wire button_1_out, clock_1_out, not_1_out, put_1_halt, put_1_put, r_or_i_1_isi;
  wire [2:0] operation_decoder_1_alu;
  wire [3:0] put_new_1_led0, put_new_1_led1, put_new_1_led2, put_new_1_led3;
  wire [7:0] adder_1_out, multiplexer_1_out, PC_q;
  wire [15:0] registers_1_read_1, rom_1_data;

  not not_1 (not_1_out, put_1_halt);
  Clock clock_1 (.out(clock_1_out));
  Button button_1 (.out(button_1_out));
  Multiplexer #(.width(8), .enable("false")) multiplexer_1 (
    .in0(adder_1_out), .out(multiplexer_1_out), .sel(1'b0));  // open: in1
  Register PC (.D(multiplexer_1_out), .en(not_1_out), .Q(PC_q), .clk(clock_1_out), .clr(button_1_out));
  Adder adder_1 (.a(8'h1), .b(PC_q), .out(adder_1_out));  // open: cin, cout
  ROM #(.dataWidth(16)) rom_1 (.addr(PC_q), .data(rom_1_data), .sel(not_1_out));
  R_or_I r_or_i_1 (
    .OpCode3(rom_1_data[15]), .OpCode2(rom_1_data[14]), .OpCode1(rom_1_data[13]), .OpCode0(rom_1_data[12]),
    .isI(r_or_i_1_isi));  // open: isR
  Put put_1 (
    .OpCode_3(rom_1_data[15]), .OpCode_2(rom_1_data[14]), .OpCode_1(rom_1_data[13]),
    .OpCode_0(rom_1_data[12]), .Halt(put_1_halt), .Put(put_1_put));
  Operation_Decoder operation_decoder_1 (
    .OpCode2(rom_1_data[14]), .OpCode1(rom_1_data[13]), .OpCode0(rom_1_data[12]),
    .ALU(operation_decoder_1_alu));
  Controlled_Buffer #(.width(8)) controlled_buffer_1 (.in(rom_1_data[8:1]), .en(r_or_i_1_isi));  // open: out
  LED led_1 (.in(put_1_halt));
  Hex_Digit_Display hex_digit_display_1 (.value(put_new_1_led3));  // open: dp
  Registers registers_1 (
    .Read_Register_1(rom_1_data[11:9]), .Read_Register_2(rom_1_data[8:6]), .Read_1(registers_1_read_1));  // open: Write_Enable_2, Write_Enable, Write_Register, Write_Data, Clock, Read_2
  Hex_Digit_Display hex_digit_display_2 (.value(put_new_1_led2));  // open: dp
  Put_New put_new_1 (
    .Print(registers_1_read_1), .LED3(put_new_1_led3), .LED2(put_new_1_led2), .LED1(put_new_1_led1),
    .LED0(put_new_1_led0), .EnablePut(put_1_put), .Clock(clock_1_out));  // open: in_4
  ALU_New alu_new_1 (.Subop(rom_1_data[0]), .Operation(operation_decoder_1_alu));  // open: A, B, Branch, Result
  Hex_Digit_Display hex_digit_display_3 (.value(put_new_1_led0));  // open: dp
  Hex_Digit_Display hex_digit_display_4 (.value(put_new_1_led1));  // open: dp
  RAM #(.bus("separate")) ram_1 (.clk(clock_1_out));  // open: addr, din, data, str, sel, ld, clr

  // Notes on the sheet:
  //   contents of rom_1 (hex, n*v repeats v):
  //   ffff
endmodule

module Registers (
  input  [2:0] Read_Register_1,
  input  Write_Enable_2,
  input  Write_Enable,
  input  [2:0] Write_Register,
  input  [15:0] Write_Data,
  input  Clock,
  input  [2:0] Read_Register_2,
  output [15:0] Read_1,
  output [15:0] Read_2
);

  wire demultiplexer_1_out0, demultiplexer_1_out1, demultiplexer_1_out2, demultiplexer_1_out3,
       demultiplexer_1_out4, demultiplexer_1_out5, demultiplexer_1_out6, demultiplexer_1_out7, or_1_out;
  wire [15:0] demultiplexer_2_out0, demultiplexer_2_out1, demultiplexer_2_out2, demultiplexer_2_out3,
       demultiplexer_2_out4, demultiplexer_2_out5, demultiplexer_2_out6, demultiplexer_2_out7, R0_q, R1_q,
       R2_q, R3_q, R4_q, R5_q, R6_q, R7_q;

  or or_1 (or_1_out, Write_Enable_2, Write_Enable);
  Demultiplexer #(.select(3)) demultiplexer_1 (
    .out0(demultiplexer_1_out0), .out1(demultiplexer_1_out1), .out2(demultiplexer_1_out2),
    .out3(demultiplexer_1_out3), .out4(demultiplexer_1_out4), .out5(demultiplexer_1_out5),
    .out6(demultiplexer_1_out6), .out7(demultiplexer_1_out7), .in(1'b1), .sel(Write_Register), .en(or_1_out));
  Demultiplexer #(.select(3), .width(16), .enable("false")) demultiplexer_2 (
    .out0(demultiplexer_2_out0), .out1(demultiplexer_2_out1), .out2(demultiplexer_2_out2),
    .out3(demultiplexer_2_out3), .out4(demultiplexer_2_out4), .out5(demultiplexer_2_out5),
    .out6(demultiplexer_2_out6), .out7(demultiplexer_2_out7), .in(Write_Data), .sel(Write_Register));
  Register #(.width(16)) R0 (.D(demultiplexer_2_out0), .en(demultiplexer_1_out0), .Q(R0_q), .clk(Clock));  // open: clr
  Register #(.width(16)) R1 (.D(demultiplexer_2_out1), .en(demultiplexer_1_out1), .Q(R1_q), .clk(Clock));  // open: clr
  Register #(.width(16)) R2 (.D(demultiplexer_2_out2), .en(demultiplexer_1_out2), .Q(R2_q), .clk(Clock));  // open: clr
  Register #(.width(16)) R3 (.D(demultiplexer_2_out3), .en(demultiplexer_1_out3), .Q(R3_q), .clk(Clock));  // open: clr
  Register #(.width(16)) R4 (.D(demultiplexer_2_out4), .en(demultiplexer_1_out4), .Q(R4_q), .clk(Clock));  // open: clr
  Register #(.width(16)) R5 (.D(demultiplexer_2_out5), .en(demultiplexer_1_out5), .Q(R5_q), .clk(Clock));  // open: clr
  Register #(.width(16)) R6 (.D(demultiplexer_2_out6), .en(demultiplexer_1_out6), .Q(R6_q), .clk(Clock));  // open: clr
  Register #(.width(16)) R7 (.D(demultiplexer_2_out7), .en(demultiplexer_1_out7), .Q(R7_q), .clk(Clock));  // open: clr
  Multiplexer #(.select(3), .width(16), .enable("false")) multiplexer_1 (
    .in0(R0_q), .in1(R1_q), .in2(R2_q), .in3(R3_q), .in4(R4_q), .in5(R5_q), .in6(R6_q), .in7(R7_q),
    .out(Read_1), .sel(Read_Register_1));
  Multiplexer #(.select(3), .width(16), .enable("false")) multiplexer_2 (
    .in0(R0_q), .in1(R1_q), .in2(R2_q), .in3(R3_q), .in4(R4_q), .in5(R5_q), .in6(R6_q), .in7(R7_q),
    .out(Read_2), .sel(Read_Register_2));
endmodule

module Put_New (
  input  [15:0] Print,
  input  EnablePut,
  input  Clock,
  input  in_4,
  output [3:0] LED3,
  output [3:0] LED2,
  output [3:0] LED1,
  output [3:0] LED0
);

  Register #(.width(16), .trigger("falling")) register_1 (
    .D(Print), .en(EnablePut), .Q({LED3, LED2, LED1, LED0}), .clk(Clock), .clr(in_4));
endmodule

module Operation_Decoder (
  input  OpCode2,
  input  OpCode1,
  input  OpCode0,
  output [2:0] ALU
);

  wire not_1_out, not_2_out;

  not not_1 (not_1_out, OpCode1);
  not not_2 (not_2_out, OpCode0);
  and and_1 (ALU[0], not_1_out, not_2_out);

  assign ALU[2:1] = {1'b0, OpCode0};
endmodule

module ALU_New (
  input  [15:0] A,
  input  Subop,
  input  [2:0] Operation,
  input  [15:0] B,
  output Branch,
  output [15:0] Result
);

  wire comparator_1_eq, comparator_1_gt, comparator_1_lt, not_1_out;
  wire [15:0] adder_1_out, and_1_out, bit_extender_1_out, bit_extender_2_out, bit_extender_3_out,
       bit_extender_4_out, multiplexer_1_out, multiplexer_2_out, multiplexer_3_out, multiplexer_4_out,
       multiplexer_5_out, nor_1_out, shifter_1_out, shifter_2_out, subtractor_1_out;

  assign and_1_out = A & B;  // AND_Gate and_1, 16 bits wide
  assign nor_1_out = ~(A | B);  // NOR_Gate nor_1, 16 bits wide
  Multiplexer #(.width(16), .enable("false")) multiplexer_1 (
    .in0(nor_1_out), .in1(and_1_out), .out(multiplexer_1_out), .sel(Subop));
  Adder #(.width(16)) adder_1 (.a(A), .b(B), .out(adder_1_out));  // open: cin, cout
  Multiplexer #(.width(16), .enable("false")) multiplexer_2 (
    .in0(adder_1_out), .in1(subtractor_1_out), .out(multiplexer_2_out), .sel(Subop));
  Subtractor #(.width(16)) subtractor_1 (.a(A), .b(B), .out(subtractor_1_out));  // open: bin, bout
  Shifter #(.width(16)) shifter_1 (.in(A), .\dist (B[3:0]), .out(shifter_1_out));
  Multiplexer #(.width(16), .enable("false")) multiplexer_3 (
    .in0(shifter_1_out), .in1(shifter_2_out), .out(multiplexer_3_out), .sel(Subop));
  Shifter #(.width(16), .shift("lr")) shifter_2 (.in(A), .\dist (B[3:0]), .out(shifter_2_out));
  not not_1 (not_1_out, comparator_1_eq);
  Comparator #(.width(16)) comparator_1 (
    .a(A), .b(B), .gt(comparator_1_gt), .eq(comparator_1_eq), .lt(comparator_1_lt));
  assign bit_extender_1_out = {{15{1'b0}}, not_1_out};  // Bit_Extender bit_extender_1
  Multiplexer #(.width(16), .enable("false")) multiplexer_4 (
    .in0(bit_extender_1_out), .in1(bit_extender_2_out), .out(multiplexer_4_out), .sel(Subop));
  assign bit_extender_2_out = {{15{1'b0}}, comparator_1_eq};  // Bit_Extender bit_extender_2
  assign bit_extender_3_out = {{15{1'b0}}, comparator_1_gt};  // Bit_Extender bit_extender_3
  Multiplexer #(.width(16), .enable("false")) multiplexer_5 (
    .in0(bit_extender_3_out), .in1(bit_extender_4_out), .out(multiplexer_5_out), .sel(Subop));
  assign bit_extender_4_out = {{15{1'b0}}, comparator_1_lt};  // Bit_Extender bit_extender_4
  Multiplexer #(.select(3), .width(16), .enable("false")) multiplexer_6 (
    .in0(multiplexer_1_out), .in1(adder_1_out), .in2(multiplexer_2_out), .in3(multiplexer_3_out),
    .in4(multiplexer_4_out), .in5(multiplexer_5_out), .in6(multiplexer_5_out), .in7(multiplexer_5_out),
    .out(Result), .sel(Operation));
  or or_1 (Branch, Result[0], Result[0], Result[1], Result[2], Result[3], Result[4], Result[5], Result[6], Result[7], Result[8], Result[9], Result[10], Result[11], Result[12], Result[13], Result[14], Result[15]);
endmodule

module Put (
  input  OpCode_3,
  input  OpCode_2,
  input  OpCode_1,
  input  OpCode_0,
  output Halt,
  output Put
);

  wire not_1_out;

  not not_1 (not_1_out, OpCode_3);
  and and_1 (Put, OpCode_3, OpCode_2, OpCode_1, OpCode_0);
  and and_2 (Halt, not_1_out, OpCode_2, OpCode_1, OpCode_0);
endmodule

module R_or_I (
  input  OpCode3,
  input  OpCode2,
  input  OpCode1,
  input  OpCode0,
  output isR,
  output isI
);

  wire and_1_out, and_2_out, and_3_out, and_4_out, and_5_out, and_6_out, and_7_out, and_8_out, not_1_out,
       not_2_out, not_3_out, not_4_out, not_5_out, not_6_out, not_7_out, not_8_out, not_9_out;

  not not_1 (not_1_out, OpCode3);
  and and_1 (and_1_out, not_1_out, OpCode0);
  not not_2 (not_2_out, OpCode3);
  and and_2 (and_2_out, not_2_out, OpCode1);
  not not_3 (not_3_out, OpCode3);
  and and_3 (and_3_out, not_3_out, OpCode2);
  not not_4 (not_4_out, OpCode1);
  and and_4 (and_4_out, OpCode2, not_4_out, OpCode0);
  not not_5 (not_5_out, OpCode2);
  and and_5 (and_5_out, not_5_out, not_6_out, not_7_out);
  not not_6 (not_6_out, OpCode1);
  not not_7 (not_7_out, OpCode0);
  and and_6 (and_6_out, OpCode3, not_8_out);
  not not_8 (not_8_out, OpCode2);
  and and_7 (and_7_out, OpCode3, not_9_out);
  not not_9 (not_9_out, OpCode0);
  and and_8 (and_8_out, OpCode3, OpCode1);
  or or_1 (isR, and_1_out, and_2_out, and_3_out, and_4_out);
  or or_2 (isI, and_5_out, and_6_out, and_7_out, and_8_out);
endmodule

module Arithmetic_Decoder (
  input  OpCode3,
  input  OpCode2,
  input  OpCode1,
  input  OpCode0,
  input  Subop,
  output Add,
  output Sub,
  output Addi,
  output Addui,
  output Nor,
  output And
);

  wire not_1_out, not_2_out, not_3_out, not_4_out, not_5_out, not_6_out, not_7_out, not_8_out, not_9_out,
       not_10_out, not_11_out, not_12_out, not_13_out, not_14_out, not_15_out, not_16_out, not_17_out,
       not_18_out, not_19_out, not_20_out, not_21_out, not_22_out;

  not not_1 (not_1_out, OpCode3);
  not not_2 (not_2_out, OpCode2);
  not not_3 (not_3_out, OpCode1);
  not not_4 (not_4_out, OpCode3);
  not not_5 (not_5_out, OpCode2);
  not not_6 (not_6_out, OpCode1);
  not not_7 (not_7_out, Subop);
  not not_8 (not_8_out, OpCode3);
  not not_9 (not_9_out, OpCode2);
  not not_10 (not_10_out, OpCode1);
  not not_11 (not_11_out, OpCode0);
  not not_12 (not_12_out, OpCode3);
  not not_13 (not_13_out, OpCode2);
  not not_14 (not_14_out, OpCode1);
  not not_15 (not_15_out, OpCode0);
  not not_16 (not_16_out, OpCode3);
  not not_17 (not_17_out, OpCode2);
  not not_18 (not_18_out, OpCode0);
  not not_19 (not_19_out, Subop);
  not not_20 (not_20_out, OpCode3);
  not not_21 (not_21_out, OpCode2);
  not not_22 (not_22_out, OpCode0);
  and and_1 (Add, not_1_out, not_2_out, not_3_out, OpCode0, Subop);
  and and_2 (Sub, not_4_out, not_5_out, not_6_out, OpCode0, not_7_out);
  and and_3 (Addi, not_8_out, not_9_out, not_10_out, not_11_out);
  and and_4 (Addui, not_12_out, not_13_out, not_14_out, not_15_out);
  and and_5 (Nor, not_16_out, not_17_out, OpCode1, not_18_out, not_19_out);
  and and_6 (And, not_20_out, not_21_out, OpCode1, not_22_out, Subop);
endmodule

module _1_bit_ALU (
  input  Carryin,
  input  A,
  input  AInvert,
  input  B,
  input  BInvert,
  input  Less,
  input  [1:0] Operation,
  output Result,
  output Set,
  output CarryOut
);

  wire and_1_out, multiplexer_1_out, multiplexer_2_out, nor_1_out, not_1_out, not_2_out;

  not not_1 (not_1_out, A);
  not not_2 (not_2_out, B);
  Multiplexer multiplexer_1 (.in0(A), .in1(not_1_out), .out(multiplexer_1_out), .sel(AInvert));  // open: en
  Multiplexer multiplexer_2 (.in0(B), .in1(not_2_out), .out(multiplexer_2_out), .sel(BInvert));  // open: en
  and and_1 (and_1_out, multiplexer_1_out, multiplexer_2_out);
  nor nor_1 (nor_1_out, multiplexer_1_out, multiplexer_2_out);
  Adder #(.width(1)) adder_1 (.a(multiplexer_1_out), .b(multiplexer_2_out), .out(Set), .cin(Carryin), .cout(CarryOut));
  Multiplexer #(.select(2)) multiplexer_3 (
    .in0(and_1_out), .in1(nor_1_out), .in2(Set), .in3(Less), .out(Result), .sel(Operation));  // open: en
endmodule

module _16_bit_ALU (
  input  A_INV,
  input  B_INV,
  input  C_IN,
  input  [1:0] Operation,
  input  [15:0] A,
  input  [15:0] Result,
  input  [15:0] B,
  output Zero,
  output Overflow
);

  wire n1_bit_alu_1_carryout, n1_bit_alu_2_carryout, n1_bit_alu_3_carryout, n1_bit_alu_4_carryout,
       n1_bit_alu_5_carryout, n1_bit_alu_6_carryout, n1_bit_alu_7_carryout, n1_bit_alu_8_carryout,
       n1_bit_alu_9_carryout, n1_bit_alu_10_carryout, n1_bit_alu_11_carryout, n1_bit_alu_12_carryout,
       n1_bit_alu_13_carryout, n1_bit_alu_14_carryout, n1_bit_alu_15_carryout, n1_bit_alu_16_carryout,
       n1_bit_alu_16_set;

  _1_bit_ALU u_1_bit_alu_1 (
    .Carryin(C_IN), .A(A[0]), .AInvert(A_INV), .B(B[0]), .BInvert(B_INV), .Less(n1_bit_alu_16_set),
    .Operation(Operation), .Result(Result[0]), .CarryOut(n1_bit_alu_1_carryout));  // open: Set
  _1_bit_ALU u_1_bit_alu_2 (
    .Carryin(n1_bit_alu_1_carryout), .A(A[1]), .AInvert(A_INV), .B(B[1]), .BInvert(B_INV), .Less(1'b0),
    .Operation(Operation), .Result(Result[1]), .CarryOut(n1_bit_alu_2_carryout));  // open: Set
  _1_bit_ALU u_1_bit_alu_3 (
    .Carryin(n1_bit_alu_2_carryout), .A(A[2]), .AInvert(A_INV), .B(B[2]), .BInvert(B_INV), .Less(1'b0),
    .Operation(Operation), .Result(Result[2]), .CarryOut(n1_bit_alu_3_carryout));  // open: Set
  _1_bit_ALU u_1_bit_alu_4 (
    .Carryin(n1_bit_alu_3_carryout), .A(A[3]), .AInvert(A_INV), .B(B[3]), .BInvert(B_INV), .Less(1'b0),
    .Operation(Operation), .Result(Result[3]), .CarryOut(n1_bit_alu_4_carryout));  // open: Set
  _1_bit_ALU u_1_bit_alu_5 (
    .Carryin(n1_bit_alu_4_carryout), .A(A[4]), .AInvert(A_INV), .B(B[4]), .BInvert(B_INV), .Less(1'b0),
    .Operation(Operation), .Result(Result[4]), .CarryOut(n1_bit_alu_5_carryout));  // open: Set
  _1_bit_ALU u_1_bit_alu_6 (
    .Carryin(n1_bit_alu_5_carryout), .A(A[5]), .AInvert(A_INV), .B(B[5]), .BInvert(B_INV), .Less(1'b0),
    .Operation(Operation), .Result(Result[5]), .CarryOut(n1_bit_alu_6_carryout));  // open: Set
  _1_bit_ALU u_1_bit_alu_7 (
    .Carryin(n1_bit_alu_6_carryout), .A(A[6]), .AInvert(A_INV), .B(B[6]), .BInvert(B_INV), .Less(1'b0),
    .Operation(Operation), .Result(Result[6]), .CarryOut(n1_bit_alu_7_carryout));  // open: Set
  _1_bit_ALU u_1_bit_alu_8 (
    .Carryin(n1_bit_alu_7_carryout), .A(A[7]), .AInvert(A_INV), .B(B[7]), .BInvert(B_INV), .Less(1'b0),
    .Operation(Operation), .Result(Result[7]), .CarryOut(n1_bit_alu_8_carryout));  // open: Set
  _1_bit_ALU u_1_bit_alu_9 (
    .Carryin(n1_bit_alu_8_carryout), .A(A[8]), .AInvert(A_INV), .B(B[8]), .BInvert(B_INV), .Less(1'b0),
    .Operation(Operation), .Result(Result[8]), .CarryOut(n1_bit_alu_9_carryout));  // open: Set
  _1_bit_ALU u_1_bit_alu_10 (
    .Carryin(n1_bit_alu_9_carryout), .A(A[9]), .AInvert(A_INV), .B(B[9]), .BInvert(B_INV), .Less(1'b0),
    .Operation(Operation), .Result(Result[9]), .CarryOut(n1_bit_alu_10_carryout));  // open: Set
  _1_bit_ALU u_1_bit_alu_11 (
    .Carryin(n1_bit_alu_10_carryout), .A(A[10]), .AInvert(A_INV), .B(B[10]), .BInvert(B_INV), .Less(1'b0),
    .Operation(Operation), .Result(Result[10]), .CarryOut(n1_bit_alu_11_carryout));  // open: Set
  _1_bit_ALU u_1_bit_alu_12 (
    .Carryin(n1_bit_alu_11_carryout), .A(A[11]), .AInvert(A_INV), .B(B[11]), .BInvert(B_INV), .Less(1'b0),
    .Operation(Operation), .Result(Result[11]), .CarryOut(n1_bit_alu_12_carryout));  // open: Set
  _1_bit_ALU u_1_bit_alu_13 (
    .Carryin(n1_bit_alu_12_carryout), .A(A[12]), .AInvert(A_INV), .B(B[12]), .BInvert(B_INV), .Less(1'b0),
    .Operation(Operation), .Result(Result[12]), .CarryOut(n1_bit_alu_13_carryout));  // open: Set
  _1_bit_ALU u_1_bit_alu_14 (
    .Carryin(n1_bit_alu_13_carryout), .A(A[13]), .AInvert(A_INV), .B(B[13]), .BInvert(B_INV), .Less(1'b0),
    .Operation(Operation), .Result(Result[13]), .CarryOut(n1_bit_alu_14_carryout));  // open: Set
  _1_bit_ALU u_1_bit_alu_15 (
    .Carryin(n1_bit_alu_14_carryout), .A(A[14]), .AInvert(A_INV), .B(B[14]), .BInvert(B_INV), .Less(1'b0),
    .Operation(Operation), .Result(Result[14]), .CarryOut(n1_bit_alu_15_carryout));  // open: Set
  _1_bit_ALU u_1_bit_alu_16 (
    .Carryin(n1_bit_alu_15_carryout), .A(A[15]), .AInvert(A_INV), .B(B[15]), .BInvert(B_INV), .Less(1'b0),
    .Operation(Operation), .Result(Result[15]), .Set(n1_bit_alu_16_set), .CarryOut(n1_bit_alu_16_carryout));
  xor xor_1 (Overflow, n1_bit_alu_15_carryout, n1_bit_alu_16_carryout);
  nor u_Zero (Zero, Result[0], Result[1], Result[2], Result[3], Result[4], Result[5], Result[6], Result[7], Result[8], Result[9], Result[10], Result[11], Result[12], Result[13], Result[14], Result[15]);
endmodule

module Instruction_Decoder (
  input  [15:0] Instruction,
  output Type_1,
  output Type_0,
  output Register_Write,
  output Halt,
  output Put,
  output Ins__Type
);

  Operation_Type operation_type_1 (
    .OpCode_3(Instruction[15]), .OpCode_2(Instruction[14]), .OpCode_1(Instruction[13]),
    .OpCode_0(Instruction[12]), .Type_1(Type_1), .Type_0(Type_0));
  Register_Write register_write_1 (
    .OpCode_3(Instruction[15]), .OpCode_2(Instruction[14]), .OpCode_1(Instruction[13]),
    .OpCode_0(Instruction[12]), .Sub_Op(Instruction[0]), .Reg_Write(Register_Write));
  Put put_1 (
    .OpCode_3(Instruction[15]), .OpCode_2(Instruction[14]), .OpCode_1(Instruction[13]),
    .OpCode_0(Instruction[12]), .Halt(Halt), .Put(Put));
  Control_Signals control_signals_1 (
    .OpCode_3(Instruction[15]), .OpCode_2(Instruction[14]), .OpCode_1(Instruction[13]),
    .OpCode_0(Instruction[12]), .Ins__Type(Ins__Type));  // open: Subop, A_INV, B_INV, C_IN, Op_1, Op_0
endmodule

module Split_New (
  input  [15:0] Instruction,
  output Subop,
  output [7:0] Immediate,
  output [2:0] RegisterB,
  output [2:0] RegisterA,
  output [4:0] Opcode
);


  assign Immediate = Instruction[8:1];
  assign Opcode = {Instruction[15:12], Instruction[0]};
  assign RegisterA = Instruction[11:9];
  assign RegisterB = Instruction[8:6];
  assign Subop = Instruction[0];
endmodule

module PC_Change (
  input  OpCode_3,
  input  OpCode_2,
  input  OpCode_1,
  input  OpCode_0,
  output PC_Change_1,
  output PC_Change_0
);

  wire and_2_out, and_3_out, not_1_out, not_2_out, not_3_out;

  not not_1 (not_1_out, OpCode_1);
  not not_2 (not_2_out, OpCode_0);
  and and_1 (PC_Change_0, OpCode_3, OpCode_2, not_3_out);
  not not_3 (not_3_out, OpCode_0);
  and and_2 (and_2_out, OpCode_3, OpCode_2, not_1_out, OpCode_0);
  or or_1 (PC_Change_1, and_2_out, and_3_out);
  and and_3 (and_3_out, OpCode_3, OpCode_2, OpCode_1, not_2_out);
endmodule

module Control_Signals (
  input  OpCode_3,
  input  OpCode_2,
  input  OpCode_1,
  input  OpCode_0,
  input  Subop,
  output A_INV,
  output B_INV,
  output C_IN,
  output Ins__Type,
  output Op_1,
  output Op_0
);

  wire and_2_out, and_3_out, and_4_out, and_5_out, and_6_out, and_7_out, and_8_out, and_9_out, and_10_out,
       and_11_out, not_1_out, not_2_out, not_3_out, not_4_out, not_5_out, not_6_out, not_7_out, not_8_out,
       not_9_out, not_10_out, not_11_out, not_12_out;

  not not_1 (not_1_out, OpCode_3);
  not not_2 (not_2_out, Subop);
  not not_3 (not_3_out, OpCode_3);
  not not_4 (not_4_out, OpCode_0);
  not not_5 (not_5_out, Subop);
  not not_6 (not_6_out, OpCode_3);
  not not_7 (not_7_out, OpCode_0);
  not not_8 (not_8_out, OpCode_2);
  not not_9 (not_9_out, OpCode_1);
  not not_10 (not_10_out, OpCode_0);
  not not_11 (not_11_out, OpCode_3);
  not not_12 (not_12_out, OpCode_1);
  and and_1 (A_INV, not_1_out, OpCode_1, not_2_out);
  and and_2 (and_2_out, not_3_out, not_4_out, Subop);
  and and_3 (and_3_out, OpCode_1, not_5_out);
  and and_4 (and_4_out, OpCode_3, OpCode_1);
  and and_5 (and_5_out, not_6_out, not_7_out, Subop);
  and and_6 (and_6_out, OpCode_3, OpCode_1);
  and and_7 (and_7_out, not_8_out, not_9_out, OpCode_0);
  and and_8 (and_8_out, OpCode_3, not_10_out);
  and and_9 (and_9_out, OpCode_3, OpCode_1);
  and and_10 (and_10_out, not_11_out, not_12_out);
  and and_11 (and_11_out, OpCode_3, OpCode_1);
  or or_1 (B_INV, and_2_out, and_3_out, and_4_out);
  or or_2 (C_IN, and_5_out, and_6_out);
  or or_3 (Ins__Type, and_7_out, and_8_out, and_9_out);
  or or_4 (Op_1, and_10_out, and_11_out);

  assign Op_0 = OpCode_3;
endmodule

module Operation_Type (
  input  OpCode_3,
  input  OpCode_2,
  input  OpCode_1,
  input  OpCode_0,
  output Type_1,
  output Type_0
);

  wire and_1_out, and_2_out, and_3_out, and_4_out, not_1_out, not_2_out, not_3_out, not_4_out;

  and and_1 (and_1_out, OpCode_2, not_1_out);
  not not_1 (not_1_out, OpCode_1);
  and and_2 (and_2_out, OpCode_3, OpCode_2, not_2_out);
  not not_2 (not_2_out, OpCode_0);
  and and_3 (and_3_out, OpCode_2, OpCode_1, not_3_out);
  not not_3 (not_3_out, OpCode_0);
  and and_4 (and_4_out, OpCode_3, OpCode_2, not_4_out);
  not not_4 (not_4_out, OpCode_1);
  or or_1 (Type_1, and_1_out, and_2_out);
  or or_2 (Type_0, and_3_out, and_4_out);
endmodule

module Branch_ID (
  input  OpCode_3,
  input  OpCode_2,
  input  OpCode_1,
  input  OpCode_0,
  output Is_Branch,
  output Branch_1,
  output Branch_0
);

  wire not_1_out, not_2_out, not_3_out;

  and and_1 (Is_Branch, OpCode_3, not_1_out);
  not not_1 (not_1_out, OpCode_2);
  not not_2 (not_2_out, OpCode_2);
  and and_2 (Branch_1, OpCode_3, not_2_out, OpCode_1);
  and and_3 (Branch_0, OpCode_3, not_3_out, OpCode_0);
  not not_3 (not_3_out, OpCode_2);
endmodule

module Shift (
  input  OpCode_3,
  input  OpCode_2,
  input  OpCode_1,
  input  OpCode_0,
  input  Sub_Op,
  output Shift,
  output ShiftRT_Shamt,
  output SR
);

  wire not_1_out, not_2_out, not_3_out, not_4_out, not_5_out, not_6_out;

  not not_1 (not_1_out, OpCode_3);
  not not_2 (not_2_out, OpCode_1);
  not not_3 (not_3_out, OpCode_3);
  not not_4 (not_4_out, OpCode_1);
  not not_5 (not_5_out, OpCode_3);
  not not_6 (not_6_out, OpCode_1);
  and and_1 (Shift, not_1_out, OpCode_2, not_2_out);
  and and_2 (ShiftRT_Shamt, not_3_out, OpCode_2, not_4_out, OpCode_0);
  and and_3 (SR, not_5_out, OpCode_2, not_6_out, Sub_Op);
endmodule

module Memory_Op (
  input  OpCode_3,
  input  OpCode_2,
  input  OpCode_1,
  input  OpCode_0,
  input  Sub_Op,
  output Load,
  output Store
);

  wire not_1_out, not_2_out, not_3_out, not_4_out, not_5_out;

  not not_1 (not_1_out, OpCode_3);
  not not_2 (not_2_out, OpCode_0);
  not not_3 (not_3_out, Sub_Op);
  not not_4 (not_4_out, OpCode_3);
  not not_5 (not_5_out, OpCode_0);
  and and_1 (Load, not_1_out, OpCode_2, OpCode_1, not_2_out, not_3_out);
  and and_2 (Store, not_4_out, OpCode_2, OpCode_1, not_5_out, Sub_Op);
endmodule

module Register_Write (
  input  OpCode_3,
  input  OpCode_2,
  input  OpCode_1,
  input  OpCode_0,
  input  Sub_Op,
  output Reg_Write
);

  wire and_1_out, and_2_out, and_3_out, and_4_out, not_1_out, not_2_out, not_3_out, not_4_out, not_5_out,
       not_6_out, not_7_out, not_8_out, not_9_out;

  not not_1 (not_1_out, OpCode_3);
  not not_2 (not_2_out, OpCode_1);
  not not_3 (not_3_out, OpCode_3);
  not not_4 (not_4_out, OpCode_2);
  not not_5 (not_5_out, OpCode_3);
  not not_6 (not_6_out, OpCode_0);
  not not_7 (not_7_out, Sub_Op);
  not not_8 (not_8_out, OpCode_1);
  not not_9 (not_9_out, OpCode_0);
  and and_1 (and_1_out, not_1_out, not_2_out);
  and and_2 (and_2_out, not_3_out, not_4_out, OpCode_0);
  and and_3 (and_3_out, not_5_out, OpCode_2, not_6_out, not_7_out);
  and and_4 (and_4_out, OpCode_2, not_8_out, not_9_out);
  or or_1 (Reg_Write, and_1_out, and_2_out, and_3_out, and_4_out);
endmodule

module Jump (
  input  OpCode_3,
  input  OpCode_2,
  input  OpCode_1,
  input  OpCode_0,
  output Jump
);

  wire and_1_out, and_2_out, not_1_out, not_2_out;

  and and_1 (and_1_out, OpCode_3, OpCode_2, not_1_out);
  not not_1 (not_1_out, OpCode_1);
  and and_2 (and_2_out, OpCode_3, OpCode_2, not_2_out);
  not not_2 (not_2_out, OpCode_0);
  or or_1 (Jump, and_1_out, and_2_out);
endmodule
