// Logisim project aep65_Lab10Part1.circ as structural Verilog: 1 circuit, main circuit main
module main (
  input  [1:0] ReadRegister1,
  input  [15:0] WriteData,
  input  WriteEnable,
  input  [1:0] WriteRegister,
  input  [1:0] ReadRegister2,
  output [15:0] ReadData1,
  output [15:0] ReadData2
);

  wire clock_1_out, decoder_1_out0, decoder_1_out1, decoder_1_out2, decoder_1_out3;
  wire [15:0] r0_q, r1_q, r2_q, r3_q;

  Decoder #(.select(2), .disabled(0)) decoder_1 (
    .out0(decoder_1_out0), .out1(decoder_1_out1), .out2(decoder_1_out2), .out3(decoder_1_out3),
    .sel(WriteRegister), .en(WriteEnable));
  Clock clock_1 (.out(clock_1_out));
  Register #(.width(16)) r0 (.D(WriteData), .en(decoder_1_out0), .Q(r0_q), .clk(clock_1_out));  // open: clr
  Register #(.width(16)) r1 (.en(decoder_1_out1), .Q(r1_q), .clk(clock_1_out));  // open: D, clr
  Register #(.width(16)) r2 (.D(WriteData), .en(decoder_1_out2), .Q(r2_q), .clk(clock_1_out));  // open: clr
  Register #(.width(16)) r3 (.D(WriteData), .en(decoder_1_out3), .Q(r3_q), .clk(clock_1_out));  // open: clr
  Multiplexer #(.select(2), .width(16)) multiplexer_1 (
    .in0(r0_q), .in1(r1_q), .in2(r2_q), .in3(r3_q), .out(ReadData1), .sel(ReadRegister1));  // open: en
  Multiplexer #(.select(2), .width(16)) multiplexer_2 (
    .in0(r0_q), .in1(r1_q), .in2(r2_q), .in3(r3_q), .out(ReadData2), .sel(ReadRegister2));  // open: en
endmodule
