// Logisim project jrmips3.circ as structural Verilog: 15 circuits, main circuit main
module main (
);

  wire alu_control_1_ainvert, alu_control_1_binvert, alu_control_1_carryin, BranchType_isbranch, Clock_out,
       controlled_buffer_4_out, d_ff_1_q, decoder_1_out1, Instruction_Type_type, jumplogic_1_isjump,
       memoptype_1_isload, memoptype_1_isstore, multiplexer_1_out, multiplexer_3_out, multiplexer_18_out,
       n16bit_alu_1_zero, nand_1_out, not_1_out, not_2_out, not_3_out, not_4_out, not_5_out, or_1_out,
       put_or_halt_1_is_halt, put_or_halt_1_is_put, regwrite_1_regwriteenable, shiftlog_1_isshift,
       shiftlog_1_shiftright, shiftlog_1_shiftrt_or_shamt;
  wire [1:0] alu_control_1_op_0, BranchType_branchtype_0, mainoptype_1_optype_0, pc_update_type_1_pc_change_0;
  wire [2:0] demultiplexer_2_out0_2, demultiplexer_2_out0_3, demultiplexer_2_out2, demultiplexer_2_out2_3,
       demultiplexer_2_out3_2, multiplexer_2_out, multiplexer_5_out, multiplexer_6_out, multiplexer_9_out,
       multiplexer_10_out, multiplexer_11_out, multiplexer_12_out, multiplexer_13_out, multiplexer_14_out;
  wire [3:0] bitselector_2_out, demultiplexer_2_out2_2, multiplexer_7_out, register_1_q, register_1_q_2;
  wire [5:0] demultiplexer_2_out0;
  wire [7:0] adder_1_out, bitselector_1_out, bitselector_3_out, controlled_buffer_1_out,
       demultiplexer_1_out1, demultiplexer_2_out3, multiplexer_4_out, multiplexer_8_out, Program_Counter_q,
       register_1_q_3;
  wire [15:0] bit_extender_1_out, bit_extender_2_out, bit_extender_3_out, controlled_buffer_2_out,
       controlled_buffer_3_out, demultiplexer_2_out1, demultiplexer_2_out2_4, multiplexer_15_out,
       multiplexer_16_out, multiplexer_17_out, multiplexer_19_out, multiplexer_20_out, multiplexer_21_out,
       multiplexer_22_out, multiplexer_23_out, multiplexer_24_out, n16bit_alu_1_result, ram_1_data,
       registerfile_8_16bit_registers_1_read_data_1, registerfile_8_16bit_registers_1_read_data_2,
       rom_1_data, shifter_1_out, shifter_2_out;
  wire [15:8] demultiplexer_2_out3_3;
  wire [15:12] demultiplexer_2_out0_4;

  Multiplexer multiplexer_1 (
    .in0(Clock_out), .in1(not_1_out), .out(multiplexer_1_out), .sel(memoptype_1_isstore));  // open: en
  not not_1 (not_1_out, Clock_out);
  Multiplexer #(.width(3), .enable("false")) multiplexer_2 (
    .in0(demultiplexer_2_out0_3), .in1(demultiplexer_2_out2), .out(multiplexer_2_out),
    .sel(shiftlog_1_isshift));
  Multiplexer multiplexer_3 (
    .in0(1'b0), .in1(multiplexer_18_out), .out(multiplexer_3_out), .sel(BranchType_isbranch));  // open: en
  Multiplexer #(.width(8)) multiplexer_4 (
    .in0(adder_1_out), .in1({demultiplexer_2_out0_2[1:0], demultiplexer_2_out0}), .out(multiplexer_4_out),
    .sel(multiplexer_3_out));  // open: en
  Clock Clock (.out(Clock_out));
  Demultiplexer #(.width(8), .enable("false")) demultiplexer_1 (
    .out1(demultiplexer_1_out1), .in(bitselector_1_out), .sel(or_1_out));  // open: out0
  BitSelector #(.width(16), .group(8)) bitselector_1 (
    .in(registerfile_8_16bit_registers_1_read_data_2), .out(bitselector_1_out), .sel(1'b0));
  Multiplexer #(.width(3), .enable("false")) multiplexer_5 (
    .in0(demultiplexer_2_out0_2), .in1(demultiplexer_2_out2_3), .out(multiplexer_5_out),
    .sel(shiftlog_1_isshift));
  Multiplexer #(.width(3), .enable("false")) multiplexer_6 (
    .in0(demultiplexer_2_out0_3), .in1(demultiplexer_2_out2), .out(multiplexer_6_out),
    .sel(shiftlog_1_isshift));
  Multiplexer #(.width(4)) multiplexer_7 (
    .in0(bitselector_2_out), .in1(demultiplexer_2_out2_2), .out(multiplexer_7_out),
    .sel(shiftlog_1_shiftrt_or_shamt));  // open: en
  Multiplexer #(.select(2), .width(8), .enable("false")) multiplexer_8 (
    .in0(multiplexer_4_out), .in1(demultiplexer_2_out3), .in2(bitselector_3_out), .in3(demultiplexer_2_out3),
    .out(multiplexer_8_out), .sel(pc_update_type_1_pc_change_0));
  Multiplexer #(.width(3), .enable("false")) multiplexer_9 (
    .in0(multiplexer_2_out), .in1(demultiplexer_2_out1[11:9]), .out(multiplexer_9_out), .sel(or_1_out));
  Multiplexer #(.width(3), .enable("false")) multiplexer_10 (
    .in0(multiplexer_5_out), .in1(demultiplexer_2_out1[8:6]), .out(multiplexer_10_out), .sel(or_1_out));
  Multiplexer #(.width(3), .enable("false")) multiplexer_11 (
    .in0(multiplexer_6_out), .in1(demultiplexer_2_out1[11:9]), .out(multiplexer_11_out), .sel(or_1_out));
  ShiftLog shiftlog_1 (
    .Opcode_3(demultiplexer_2_out2_4[15]), .Opcode_2(demultiplexer_2_out2_4[14]),
    .Opcode_1(demultiplexer_2_out2_4[13]), .Opcode_0(demultiplexer_2_out2_4[12]),
    .Subop(demultiplexer_2_out2_4[0]), .isShift(shiftlog_1_isshift),
    .shiftRT_or_shamt(shiftlog_1_shiftrt_or_shamt), .shiftRight(shiftlog_1_shiftright));
  Shifter #(.width(16)) shifter_1 (
    .in(registerfile_8_16bit_registers_1_read_data_1), .\dist (multiplexer_7_out), .out(shifter_1_out));
  Shifter #(.width(16), .shift("lr")) shifter_2 (
    .in(registerfile_8_16bit_registers_1_read_data_1), .\dist (multiplexer_7_out), .out(shifter_2_out));
  BitSelector #(.width(16), .group(4)) bitselector_2 (
    .in(registerfile_8_16bit_registers_1_read_data_2), .out(bitselector_2_out), .sel(2'b00));
  Adder adder_1 (.a(Program_Counter_q), .b(8'h1), .out(adder_1_out));  // open: cin, cout
  Register Program_Counter (.D(multiplexer_8_out), .Q(Program_Counter_q), .clk(d_ff_1_q));  // open: en, clr
  not not_2 (not_2_out, Clock_out);
  Multiplexer #(.width(3), .enable("false")) multiplexer_12 (
    .in0(multiplexer_9_out), .in1(demultiplexer_2_out3_2), .out(multiplexer_12_out), .sel(jumplogic_1_isjump));
  Multiplexer #(.width(3), .enable("false")) multiplexer_13 (
    .in0(multiplexer_10_out), .in1(demultiplexer_2_out3_2), .out(multiplexer_13_out), .sel(jumplogic_1_isjump));
  Multiplexer #(.width(3), .enable("false")) multiplexer_14 (
    .in0(multiplexer_11_out), .in1(demultiplexer_2_out3_2), .out(multiplexer_14_out), .sel(jumplogic_1_isjump));
  Multiplexer #(.width(16), .enable("false")) multiplexer_15 (
    .in0(multiplexer_17_out), .in1(bit_extender_1_out), .out(multiplexer_15_out), .sel(jumplogic_1_isjump));
  Multiplexer #(.width(16), .enable("false")) multiplexer_16 (
    .in0(shifter_1_out), .in1(shifter_2_out), .out(multiplexer_16_out), .sel(shiftlog_1_shiftright));
  assign controlled_buffer_1_out = Clock_out ? Program_Counter_q : 8'bz;  // Controlled_Buffer controlled_buffer_1
  D_Flip_Flop #(.trigger("low")) d_ff_1 (.clk(Clock_out), .D(not_2_out), .Q(d_ff_1_q));  // open: Qn, preset, en, reset
  RAM #(.dataWidth(16), .bus("separate")) ram_1 (
    .addr(demultiplexer_1_out1), .din(registerfile_8_16bit_registers_1_read_data_1), .data(ram_1_data),
    .str(memoptype_1_isstore), .sel(or_1_out), .clk(multiplexer_1_out), .ld(memoptype_1_isload));  // open: clr
  Decoder decoder_1 (.out1(decoder_1_out1), .sel(regwrite_1_regwriteenable));  // open: out0, en
  RegisterFile_8_16bit_Registers registerfile_8_16bit_registers_1 (
    .Read_Register_1(multiplexer_12_out), .Read_Register_2(multiplexer_13_out),
    .Write_Register(multiplexer_14_out), .Write_Data(multiplexer_15_out),
    .Read_Data_1(registerfile_8_16bit_registers_1_read_data_1),
    .Read_Data_2(registerfile_8_16bit_registers_1_read_data_2), .writeEnabled(decoder_1_out1),
    .Clock(not_3_out));
  Multiplexer #(.width(16), .enable("false")) multiplexer_17 (
    .in0(multiplexer_23_out), .in1(multiplexer_16_out), .out(multiplexer_17_out), .sel(shiftlog_1_isshift));
  not not_3 (not_3_out, Clock_out);
  nand nand_1 (nand_1_out, 1'b1, put_or_halt_1_is_halt);
  JumpLogic jumplogic_1 (
    .Opcode_3(demultiplexer_2_out3_3[15]), .Opcode_2(demultiplexer_2_out3_3[14]),
    .Opcode_1(demultiplexer_2_out3_3[13]), .Opcode_0(demultiplexer_2_out3_3[12]), .isJump(jumplogic_1_isjump));
  PC_Update_Type pc_update_type_1 (
    .Opcode_3(demultiplexer_2_out3_3[15]), .Opcode_2(demultiplexer_2_out3_3[14]),
    .Opcode_1(demultiplexer_2_out3_3[13]), .Opcode_0(demultiplexer_2_out3_3[12]),
    .PC_Change_1(pc_update_type_1_pc_change_0[1]), .PC_Change_0(pc_update_type_1_pc_change_0[0]));
  or or_1 (or_1_out, memoptype_1_isstore, memoptype_1_isload);
  Multiplexer #(.select(2)) multiplexer_18 (
    .in0(n16bit_alu_1_zero), .in1(not_4_out), .in2(not_4_out), .in3(not_4_out), .out(multiplexer_18_out),
    .sel(BranchType_branchtype_0));  // open: en
  BitSelector #(.width(16), .group(8)) bitselector_3 (
    .in(registerfile_8_16bit_registers_1_read_data_1), .out(bitselector_3_out), .sel(1'b0));
  assign bit_extender_1_out = {{8{1'b0}}, adder_1_out};  // Bit_Extender bit_extender_1
  ROM #(.dataWidth(16)) rom_1 (.addr(controlled_buffer_1_out), .data(rom_1_data), .sel(nand_1_out));
  Multiplexer #(.width(16)) multiplexer_19 (
    .in0(registerfile_8_16bit_registers_1_read_data_2), .in1(multiplexer_24_out), .out(multiplexer_19_out),
    .sel(Instruction_Type_type));  // open: en
  not not_4 (not_4_out, n16bit_alu_1_zero);
  Demultiplexer #(.select(2), .width(16)) demultiplexer_2 (
    .out0({demultiplexer_2_out0_4, demultiplexer_2_out0_3, demultiplexer_2_out0_2, demultiplexer_2_out0}),
    .out1(demultiplexer_2_out1),
    .out2({demultiplexer_2_out2_4[15:12], demultiplexer_2_out2, demultiplexer_2_out2_3, demultiplexer_2_out2_4[5], demultiplexer_2_out2_2, demultiplexer_2_out2_4[0]}),
    .out3({demultiplexer_2_out3_3[15:12], demultiplexer_2_out3_2, demultiplexer_2_out3_3[8], demultiplexer_2_out3}),
    .in(rom_1_data), .sel(mainoptype_1_optype_0));  // open: en
  assign controlled_buffer_2_out = not_5_out ? registerfile_8_16bit_registers_1_read_data_1 : 16'bz;  // Controlled_Buffer controlled_buffer_2
  assign controlled_buffer_3_out = not_5_out ? multiplexer_19_out : 16'bz;  // Controlled_Buffer controlled_buffer_3
  not not_5 (not_5_out, BranchType_isbranch);
  Multiplexer #(.select(2), .width(16)) multiplexer_20 (
    .in0(registerfile_8_16bit_registers_1_read_data_1), .in1(registerfile_8_16bit_registers_1_read_data_1),
    .in2({16{1'b0}}), .in3(registerfile_8_16bit_registers_1_read_data_1), .out(multiplexer_20_out),
    .sel(BranchType_branchtype_0));  // open: en
  Multiplexer #(.width(16)) multiplexer_21 (
    .in0(registerfile_8_16bit_registers_1_read_data_1), .in1({16{1'b0}}), .out(multiplexer_21_out),
    .sel(BranchType_branchtype_0[0]));  // open: en
  MainOpType mainoptype_1 (
    .Opcode_3(rom_1_data[15]), .Opcode_2(rom_1_data[14]), .Opcode_1(rom_1_data[13]),
    .Opcode_0(rom_1_data[12]), .OpType_1(mainoptype_1_optype_0[1]), .OpType_0(mainoptype_1_optype_0[0]));
  RegWrite regwrite_1 (
    .Opcode_3(rom_1_data[15]), .Opcode_2(rom_1_data[14]), .Opcode_1(rom_1_data[13]),
    .Opcode_0(rom_1_data[12]), .Subop(rom_1_data[0]), .RegWriteEnable(regwrite_1_regwriteenable));
  put_or_halt put_or_halt_1 (
    .Opcode_3(rom_1_data[15]), .Opcode_2(rom_1_data[14]), .Opcode_1(rom_1_data[13]),
    .Opcode_0(rom_1_data[12]), .is_halt(put_or_halt_1_is_halt), .is_put(put_or_halt_1_is_put));
  I_OR_R Instruction_Type (
    .Opcode_3(rom_1_data[15]), .Opcode_2(rom_1_data[14]), .Opcode_1(rom_1_data[13]),
    .Opcode_0(rom_1_data[12]), .Type(Instruction_Type_type));
  assign controlled_buffer_4_out = put_or_halt_1_is_put ? Clock_out : 1'bz;  // Controlled_Buffer controlled_buffer_4
  assign controlled_buffer_2_out = BranchType_isbranch ? multiplexer_20_out : 16'bz;  // Controlled_Buffer controlled_buffer_5
  Multiplexer #(.width(16)) multiplexer_22 (
    .in0(multiplexer_20_out), .in1(multiplexer_21_out), .out(multiplexer_22_out),
    .sel(BranchType_branchtype_0[1]));  // open: en
  assign controlled_buffer_3_out = BranchType_isbranch ? multiplexer_22_out : 16'bz;  // Controlled_Buffer controlled_buffer_6
  branchType BranchType (
    .Opcode_3(demultiplexer_2_out0_4[15]), .Opcode_2(demultiplexer_2_out0_4[14]),
    .Opcode_1(demultiplexer_2_out0_4[13]), .Opcode_0(demultiplexer_2_out0_4[12]),
    .isBranch(BranchType_isbranch), .BranchType_1(BranchType_branchtype_0[1]),
    .BranchType_0(BranchType_branchtype_0[0]));
  LED led_1 (.in(put_or_halt_1_is_halt));
  ALU_Control alu_control_1 (
    .OpCode_3(demultiplexer_2_out0_4[15]), .OpCode_2(demultiplexer_2_out0_4[14]),
    .OpCode_1(demultiplexer_2_out0_4[13]), .OpCode_0(demultiplexer_2_out0_4[12]),
    .Subop(demultiplexer_2_out0[0]), .Ainvert(alu_control_1_ainvert), .Binvert(alu_control_1_binvert),
    .CarryIn(alu_control_1_carryin), .Op_1(alu_control_1_op_0[1]), .Op_0(alu_control_1_op_0[0]));
  MemOpType memoptype_1 (
    .Opcode_3(demultiplexer_2_out1[15]), .Opcode_2(demultiplexer_2_out1[14]),
    .Opcode_1(demultiplexer_2_out1[13]), .Opcode_0(demultiplexer_2_out1[12]),
    .Subop(demultiplexer_2_out1[0]), .isLoad(memoptype_1_isload), .isStore(memoptype_1_isstore));
  _16bit_ALU u_16bit_alu_1 (
    .A(controlled_buffer_2_out), .B(controlled_buffer_3_out), .Zero(n16bit_alu_1_zero),
    .Result(n16bit_alu_1_result), .Ainvert(alu_control_1_ainvert), .Binvert(alu_control_1_binvert),
    .CarryIn(alu_control_1_carryin), .Operation(alu_control_1_op_0));  // open: Overfow
  Multiplexer #(.width(16), .enable("false")) multiplexer_23 (
    .in0(n16bit_alu_1_result), .in1(ram_1_data), .out(multiplexer_23_out), .sel(memoptype_1_isload));
  assign bit_extender_2_out = {{8{demultiplexer_2_out0_2[1]}}, {demultiplexer_2_out0_2[1:0], demultiplexer_2_out0}};  // Bit_Extender bit_extender_2
  assign bit_extender_3_out = {{8{1'b0}}, {demultiplexer_2_out0_2[1:0], demultiplexer_2_out0}};  // Bit_Extender bit_extender_3
  Hex_Digit_Display hex_digit_display_1 (.value(register_1_q_2));  // open: dp
  Hex_Digit_Display hex_digit_display_2 (.value(register_1_q));  // open: dp
  Register #(.width(16), .trigger("falling")) register_1 (
    .D(registerfile_8_16bit_registers_1_read_data_1), .en(1'b1),
    .Q({register_1_q_2, register_1_q, register_1_q_3}), .clk(controlled_buffer_4_out));  // open: clr
  Multiplexer #(.width(16)) multiplexer_24 (
    .in0(bit_extender_2_out), .in1(bit_extender_3_out), .out(multiplexer_24_out),
    .sel(demultiplexer_2_out0_2[2]));  // open: en
  Hex_Digit_Display hex_digit_display_3 (.value(register_1_q_3[3:0]));  // open: dp
  Hex_Digit_Display hex_digit_display_4 (.value(register_1_q_3[7:4]));  // open: dp

  // Notes on the sheet:
  //   Shifts
  //   Registers
  //   contents of rom_1 (hex, n*v repeats v):
  //   1000 f000 2 1240 1201 3e0 a202 7000
  //   HALT LED
  //   rs
  //   ALU
endmodule

module _16bit_ALU (
  input  Ainvert,
  input  Binvert,
  input  CarryIn,
  input  [1:0] Operation,
  input  [15:0] A,
  input  [15:0] B,
  output Zero,
  output [15:0] Result,
  output Overfow
);

  wire n1_bit_alu_1_carryout, n1_bit_alu_2_carryout, n1_bit_alu_3_carryout, n1_bit_alu_4_carryout,
       n1_bit_alu_5_carryout, n1_bit_alu_6_carryout, n1_bit_alu_7_carryout, n1_bit_alu_8_carryout,
       n1_bit_alu_9_carryout, n1_bit_alu_10_carryout, n1_bit_alu_11_carryout, n1_bit_alu_12_carryout,
       n1_bit_alu_13_carryout, n1_bit_alu_14_carryout, n1_bit_alu_15_carryout, n1_bit_alu_set_1_set;

  _1_bit_ALU u_1_bit_alu_1 (
    .a(A[0]), .b(B[0]), .Less(n1_bit_alu_set_1_set), .Result(Result[0]), .Ainvert(Ainvert),
    .Binvert(Binvert), .CarryIn(CarryIn), .Operation(Operation), .CarryOut(n1_bit_alu_1_carryout));
  _1_bit_ALU u_1_bit_alu_2 (
    .a(A[1]), .b(B[1]), .Less(1'b0), .Result(Result[1]), .Ainvert(Ainvert), .Binvert(Binvert),
    .CarryIn(n1_bit_alu_1_carryout), .Operation(Operation), .CarryOut(n1_bit_alu_2_carryout));
  _1_bit_ALU u_1_bit_alu_3 (
    .a(A[2]), .b(B[2]), .Less(1'b0), .Result(Result[2]), .Ainvert(Ainvert), .Binvert(Binvert),
    .CarryIn(n1_bit_alu_2_carryout), .Operation(Operation), .CarryOut(n1_bit_alu_3_carryout));
  _1_bit_ALU u_1_bit_alu_4 (
    .a(A[3]), .b(B[3]), .Less(1'b0), .Result(Result[3]), .Ainvert(Ainvert), .Binvert(Binvert),
    .CarryIn(n1_bit_alu_3_carryout), .Operation(Operation), .CarryOut(n1_bit_alu_4_carryout));
  _1_bit_ALU u_1_bit_alu_5 (
    .a(A[4]), .b(B[4]), .Less(1'b0), .Result(Result[4]), .Ainvert(Ainvert), .Binvert(Binvert),
    .CarryIn(n1_bit_alu_4_carryout), .Operation(Operation), .CarryOut(n1_bit_alu_5_carryout));
  _1_bit_ALU u_1_bit_alu_6 (
    .a(A[5]), .b(B[5]), .Less(1'b0), .Result(Result[5]), .Ainvert(Ainvert), .Binvert(Binvert),
    .CarryIn(n1_bit_alu_5_carryout), .Operation(Operation), .CarryOut(n1_bit_alu_6_carryout));
  _1_bit_ALU u_1_bit_alu_7 (
    .a(A[6]), .b(B[6]), .Less(1'b0), .Result(Result[6]), .Ainvert(Ainvert), .Binvert(Binvert),
    .CarryIn(n1_bit_alu_6_carryout), .Operation(Operation), .CarryOut(n1_bit_alu_7_carryout));
  _1_bit_ALU u_1_bit_alu_8 (
    .a(A[7]), .b(B[7]), .Less(1'b0), .Result(Result[7]), .Ainvert(Ainvert), .Binvert(Binvert),
    .CarryIn(n1_bit_alu_7_carryout), .Operation(Operation), .CarryOut(n1_bit_alu_8_carryout));
  _1_bit_ALU u_1_bit_alu_9 (
    .a(A[8]), .b(B[8]), .Less(1'b0), .Result(Result[8]), .Ainvert(Ainvert), .Binvert(Binvert),
    .CarryIn(n1_bit_alu_8_carryout), .Operation(Operation), .CarryOut(n1_bit_alu_9_carryout));
  _1_bit_ALU u_1_bit_alu_10 (
    .a(A[9]), .b(B[9]), .Less(1'b0), .Result(Result[9]), .Ainvert(Ainvert), .Binvert(Binvert),
    .CarryIn(n1_bit_alu_9_carryout), .Operation(Operation), .CarryOut(n1_bit_alu_10_carryout));
  _1_bit_ALU u_1_bit_alu_11 (
    .a(A[10]), .b(B[10]), .Less(1'b0), .Result(Result[10]), .Ainvert(Ainvert), .Binvert(Binvert),
    .CarryIn(n1_bit_alu_10_carryout), .Operation(Operation), .CarryOut(n1_bit_alu_11_carryout));
  _1_bit_ALU u_1_bit_alu_12 (
    .a(A[11]), .b(B[11]), .Less(1'b0), .Result(Result[11]), .Ainvert(Ainvert), .Binvert(Binvert),
    .CarryIn(n1_bit_alu_11_carryout), .Operation(Operation), .CarryOut(n1_bit_alu_12_carryout));
  _1_bit_ALU u_1_bit_alu_13 (
    .a(A[12]), .b(B[12]), .Less(1'b0), .Result(Result[12]), .Ainvert(Ainvert), .Binvert(Binvert),
    .CarryIn(n1_bit_alu_12_carryout), .Operation(Operation), .CarryOut(n1_bit_alu_13_carryout));
  _1_bit_ALU u_1_bit_alu_14 (
    .a(A[13]), .b(B[13]), .Less(1'b0), .Result(Result[13]), .Ainvert(Ainvert), .Binvert(Binvert),
    .CarryIn(n1_bit_alu_13_carryout), .Operation(Operation), .CarryOut(n1_bit_alu_14_carryout));
  _1_bit_ALU u_1_bit_alu_15 (
    .a(A[14]), .b(B[14]), .Less(1'b0), .Result(Result[14]), .Ainvert(Ainvert), .Binvert(Binvert),
    .CarryIn(n1_bit_alu_14_carryout), .Operation(Operation), .CarryOut(n1_bit_alu_15_carryout));
  _1_bit_ALU_SET u_1_bit_alu_set_1 (
    .a(A[15]), .b(B[15]), .Less(1'b0), .Result(Result[15]), .Set(n1_bit_alu_set_1_set), .Ainvert(Ainvert),
    .Binvert(Binvert), .CarryIn(n1_bit_alu_15_carryout), .Operation(Operation), .CarryOut(Overfow));
  nor nor_1 (Zero, Result[0], Result[1], Result[2], Result[3], Result[4], Result[5], Result[6], Result[7], Result[8], Result[9], Result[10], Result[11], Result[12], Result[13], Result[14], Result[15]);
endmodule

module _1_bit_ALU (
  input  Ainvert,
  input  Binvert,
  input  CarryIn,
  input  [1:0] Operation,
  input  a,
  input  b,
  input  Less,
  output Result,
  output CarryOut
);

  wire adder_1_out, and_1_out, multiplexer_1_out, multiplexer_2_out, not_1_out, not_2_out, or_1_out;

  not not_1 (not_1_out, a);
  not not_2 (not_2_out, b);
  Multiplexer multiplexer_1 (.in0(a), .in1(not_1_out), .out(multiplexer_1_out), .sel(Ainvert));  // open: en
  Multiplexer multiplexer_2 (.in0(b), .in1(not_2_out), .out(multiplexer_2_out), .sel(Binvert));  // open: en
  and and_1 (and_1_out, multiplexer_1_out, multiplexer_2_out);
  or or_1 (or_1_out, multiplexer_1_out, multiplexer_2_out);
  Adder #(.width(1)) adder_1 (
    .a(multiplexer_1_out), .b(multiplexer_2_out), .out(adder_1_out), .cin(CarryIn), .cout(CarryOut));
  Multiplexer #(.select(2)) multiplexer_3 (
    .in0(and_1_out), .in1(or_1_out), .in2(adder_1_out), .in3(Less), .out(Result), .sel(Operation));  // open: en
endmodule

module _1_bit_ALU_SET (
  input  Ainvert,
  input  Binvert,
  input  CarryIn,
  input  [1:0] Operation,
  input  a,
  input  b,
  input  Less,
  output Result,
  output Set,
  output CarryOut
);

  wire and_1_out, multiplexer_1_out, multiplexer_2_out, not_1_out, not_2_out, or_1_out;

  not not_1 (not_1_out, a);
  not not_2 (not_2_out, b);
  Multiplexer multiplexer_1 (.in0(a), .in1(not_1_out), .out(multiplexer_1_out), .sel(Ainvert));  // open: en
  Multiplexer multiplexer_2 (.in0(b), .in1(not_2_out), .out(multiplexer_2_out), .sel(Binvert));  // open: en
  and and_1 (and_1_out, multiplexer_1_out, multiplexer_2_out);
  or or_1 (or_1_out, multiplexer_1_out, multiplexer_2_out);
  Adder #(.width(1)) adder_1 (.a(multiplexer_1_out), .b(multiplexer_2_out), .out(Set), .cin(CarryIn), .cout(CarryOut));
  Multiplexer #(.select(2)) multiplexer_3 (
    .in0(and_1_out), .in1(or_1_out), .in2(Set), .in3(Less), .out(Result), .sel(Operation));  // open: en
endmodule

module RegisterFile_8_16bit_Registers (
  input  writeEnabled,
  input  [2:0] Read_Register_1,
  input  [2:0] Read_Register_2,
  input  [2:0] Write_Register,
  input  [15:0] Write_Data,
  input  Clock,
  output [15:0] Read_Data_1,
  output [15:0] Read_Data_2
);

  wire decoder_1_out0, decoder_1_out1, decoder_1_out2, decoder_1_out3, decoder_1_out4, decoder_1_out5,
       decoder_1_out6, decoder_1_out7;
  wire [15:0] demultiplexer_1_out0, demultiplexer_1_out1, demultiplexer_1_out2, demultiplexer_1_out3,
       demultiplexer_1_out4, demultiplexer_1_out5, demultiplexer_1_out6, demultiplexer_1_out7, Register_0_q,
       Register_1_q, Register_2_q, Register_3_q, Register_4_q, Register_5_q, Register_6_q, Register_7_q;

  Demultiplexer #(.select(3), .width(16)) demultiplexer_1 (
    .out0(demultiplexer_1_out0), .out1(demultiplexer_1_out1), .out2(demultiplexer_1_out2),
    .out3(demultiplexer_1_out3), .out4(demultiplexer_1_out4), .out5(demultiplexer_1_out5),
    .out6(demultiplexer_1_out6), .out7(demultiplexer_1_out7), .in(Write_Data), .sel(Write_Register));  // open: en
  Decoder #(.select(3), .disabled(0)) decoder_1 (
    .out0(decoder_1_out0), .out1(decoder_1_out1), .out2(decoder_1_out2), .out3(decoder_1_out3),
    .out4(decoder_1_out4), .out5(decoder_1_out5), .out6(decoder_1_out6), .out7(decoder_1_out7),
    .sel(Write_Register), .en(writeEnabled));
  Register #(.width(16)) Register_0 (
    .D(demultiplexer_1_out0), .en(decoder_1_out0), .Q(Register_0_q), .clk(Clock));  // open: clr
  Register #(.width(16)) Register_1 (
    .D(demultiplexer_1_out1), .en(decoder_1_out1), .Q(Register_1_q), .clk(Clock));  // open: clr
  Register #(.width(16)) Register_2 (
    .D(demultiplexer_1_out2), .en(decoder_1_out2), .Q(Register_2_q), .clk(Clock));  // open: clr
  Register #(.width(16)) Register_3 (
    .D(demultiplexer_1_out3), .en(decoder_1_out3), .Q(Register_3_q), .clk(Clock));  // open: clr
  Register #(.width(16)) Register_4 (
    .D(demultiplexer_1_out4), .en(decoder_1_out4), .Q(Register_4_q), .clk(Clock));  // open: clr
  Register #(.width(16)) Register_5 (
    .D(demultiplexer_1_out5), .en(decoder_1_out5), .Q(Register_5_q), .clk(Clock));  // open: clr
  Register #(.width(16)) Register_6 (
    .D(demultiplexer_1_out6), .en(decoder_1_out6), .Q(Register_6_q), .clk(Clock));  // open: clr
  Register #(.width(16)) Register_7 (
    .D(demultiplexer_1_out7), .en(decoder_1_out7), .Q(Register_7_q), .clk(Clock));  // open: clr
  Multiplexer #(.select(3), .width(16)) multiplexer_1 (
    .in0(Register_0_q), .in1(Register_1_q), .in2(Register_2_q), .in3(Register_3_q), .in4(Register_4_q),
    .in5(Register_5_q), .in6(Register_6_q), .in7(Register_7_q), .out(Read_Data_1), .sel(Read_Register_1));  // open: en
  Multiplexer #(.select(3), .width(16)) multiplexer_2 (
    .in0(Register_0_q), .in1(Register_1_q), .in2(Register_2_q), .in3(Register_3_q), .in4(Register_4_q),
    .in5(Register_5_q), .in6(Register_6_q), .in7(Register_7_q), .out(Read_Data_2), .sel(Read_Register_2));  // open: en
endmodule

module ALU_Control (
  input  OpCode_3,
  input  OpCode_2,
  input  OpCode_1,
  input  OpCode_0,
  input  Subop,
  output Ainvert,
  output Binvert,
  output CarryIn,
  output Op_1,
  output Op_0
);

  wire and_2_out, and_3_out, and_4_out, and_5_out, and_6_out, and_7_out, and_8_out, not_1_out, not_2_out,
       not_3_out, not_4_out, not_5_out, not_6_out, not_7_out, not_8_out, not_9_out;

  not not_1 (not_1_out, OpCode_3);
  not not_2 (not_2_out, Subop);
  not not_3 (not_3_out, OpCode_3);
  not not_4 (not_4_out, OpCode_0);
  not not_5 (not_5_out, Subop);
  not not_6 (not_6_out, OpCode_3);
  not not_7 (not_7_out, OpCode_0);
  not not_8 (not_8_out, OpCode_3);
  not not_9 (not_9_out, OpCode_1);
  and and_1 (Ainvert, not_1_out, OpCode_1, not_2_out);
  and and_2 (and_2_out, not_3_out, not_4_out, Subop);
  and and_3 (and_3_out, OpCode_1, not_5_out);
  and and_4 (and_4_out, OpCode_3, OpCode_1);
  and and_5 (and_5_out, not_6_out, not_7_out, Subop);
  and and_6 (and_6_out, OpCode_3, OpCode_1);
  and and_7 (and_7_out, not_8_out, not_9_out);
  and and_8 (and_8_out, OpCode_3, OpCode_1);
  or or_1 (Binvert, and_2_out, and_3_out, and_4_out);
  or or_2 (CarryIn, and_5_out, and_6_out);
  or or_3 (Op_1, and_7_out, and_8_out);

  assign Op_0 = OpCode_3;
endmodule

module I_OR_R (
  input  Opcode_3,
  input  Opcode_2,
  input  Opcode_1,
  input  Opcode_0,
  output Type
);

  wire and_1_out, and_2_out, and_3_out, not_1_out, not_2_out, not_3_out;

  not not_1 (not_1_out, Opcode_2);
  and and_1 (and_1_out, not_1_out, not_2_out, Opcode_0);
  not not_2 (not_2_out, Opcode_1);
  and and_2 (and_2_out, Opcode_3, not_3_out);
  not not_3 (not_3_out, Opcode_0);
  and and_3 (and_3_out, Opcode_3, Opcode_1);
  or or_1 (Type, and_1_out, and_2_out, and_3_out);
endmodule

module put_or_halt (
  input  Opcode_3,
  input  Opcode_2,
  input  Opcode_1,
  input  Opcode_0,
  output is_halt,
  output is_put
);

  wire not_1_out;

  not not_1 (not_1_out, Opcode_3);
  and and_1 (is_put, Opcode_3, Opcode_2, Opcode_1, Opcode_0);
  and and_2 (is_halt, not_1_out, Opcode_2, Opcode_1, Opcode_0);
endmodule

module RegWrite (
  input  Opcode_3,
  input  Opcode_2,
  input  Opcode_1,
  input  Opcode_0,
  input  Subop,
  output RegWriteEnable
);

  wire and_1_out, and_2_out, and_3_out, and_4_out, not_1_out, not_2_out, not_3_out, not_4_out, not_5_out,
       not_6_out, not_7_out, not_8_out, not_9_out;

  not not_1 (not_1_out, Opcode_3);
  not not_2 (not_2_out, Opcode_1);
  not not_3 (not_3_out, Opcode_3);
  not not_4 (not_4_out, Opcode_2);
  not not_5 (not_5_out, Opcode_3);
  not not_6 (not_6_out, Opcode_0);
  not not_7 (not_7_out, Subop);
  not not_8 (not_8_out, Opcode_1);
  not not_9 (not_9_out, Opcode_0);
  and and_1 (and_1_out, not_1_out, not_2_out);
  and and_2 (and_2_out, not_3_out, not_4_out, Opcode_0);
  and and_3 (and_3_out, not_5_out, Opcode_2, not_6_out, not_7_out);
  and and_4 (and_4_out, Opcode_2, not_8_out, not_9_out);
  or or_1 (RegWriteEnable, and_1_out, and_2_out, and_3_out, and_4_out);
endmodule

module branchType (
  input  Opcode_3,
  input  Opcode_2,
  input  Opcode_1,
  input  Opcode_0,
  output isBranch,
  output BranchType_1,
  output BranchType_0
);

  wire not_1_out, not_2_out, not_3_out;

  and and_1 (isBranch, Opcode_3, not_1_out);
  not not_1 (not_1_out, Opcode_2);
  not not_2 (not_2_out, Opcode_2);
  and and_2 (BranchType_1, Opcode_3, not_2_out, Opcode_1);
  and and_3 (BranchType_0, Opcode_3, not_3_out, Opcode_0);
  not not_3 (not_3_out, Opcode_2);
endmodule

module MemOpType (
  input  Opcode_3,
  input  Opcode_2,
  input  Opcode_1,
  input  Opcode_0,
  input  Subop,
  output isLoad,
  output isStore
);

  wire not_1_out, not_2_out, not_3_out, not_4_out, not_5_out;

  not not_1 (not_1_out, Opcode_3);
  not not_2 (not_2_out, Opcode_0);
  not not_3 (not_3_out, Subop);
  not not_4 (not_4_out, Opcode_3);
  not not_5 (not_5_out, Opcode_0);
  and and_1 (isLoad, not_1_out, Opcode_2, Opcode_1, not_2_out, not_3_out);
  and and_2 (isStore, not_4_out, Opcode_2, Opcode_1, not_5_out, Subop);
endmodule

module MainOpType (
  input  Opcode_3,
  input  Opcode_2,
  input  Opcode_1,
  input  Opcode_0,
  output OpType_1,
  output OpType_0
);

  wire and_1_out, and_2_out, and_3_out, and_4_out, not_1_out, not_2_out, not_3_out, not_4_out;

  and and_1 (and_1_out, Opcode_2, not_1_out);
  not not_1 (not_1_out, Opcode_1);
  and and_2 (and_2_out, Opcode_3, Opcode_2, not_2_out);
  not not_2 (not_2_out, Opcode_0);
  and and_3 (and_3_out, Opcode_2, Opcode_1, not_3_out);
  not not_3 (not_3_out, Opcode_0);
  and and_4 (and_4_out, Opcode_3, Opcode_2, not_4_out);
  not not_4 (not_4_out, Opcode_1);
  or or_1 (OpType_1, and_1_out, and_2_out);
  or or_2 (OpType_0, and_3_out, and_4_out);
endmodule

module ShiftLog (
  input  Opcode_3,
  input  Opcode_2,
  input  Opcode_1,
  input  Opcode_0,
  input  Subop,
  output isShift,
  output shiftRT_or_shamt,
  output shiftRight
);

  wire not_1_out, not_2_out, not_3_out, not_4_out, not_5_out, not_6_out;

  not not_1 (not_1_out, Opcode_3);
  not not_2 (not_2_out, Opcode_1);
  not not_3 (not_3_out, Opcode_3);
  not not_4 (not_4_out, Opcode_1);
  not not_5 (not_5_out, Opcode_3);
  not not_6 (not_6_out, Opcode_1);
  and and_1 (isShift, not_1_out, Opcode_2, not_2_out);
  and and_2 (shiftRT_or_shamt, not_3_out, Opcode_2, not_4_out, Opcode_0);
  and and_3 (shiftRight, not_5_out, Opcode_2, not_6_out, Subop);
endmodule

module JumpLogic (
  input  Opcode_3,
  input  Opcode_2,
  input  Opcode_1,
  input  Opcode_0,
  output isJump
);

  wire and_1_out, and_2_out, not_1_out, not_2_out;

  and and_1 (and_1_out, Opcode_3, Opcode_2, not_1_out);
  not not_1 (not_1_out, Opcode_1);
  and and_2 (and_2_out, Opcode_3, Opcode_2, not_2_out);
  not not_2 (not_2_out, Opcode_0);
  or or_1 (isJump, and_1_out, and_2_out);
endmodule

module PC_Update_Type (
  input  Opcode_3,
  input  Opcode_2,
  input  Opcode_1,
  input  Opcode_0,
  output PC_Change_1,
  output PC_Change_0
);

  wire and_2_out, and_3_out, not_1_out, not_2_out, not_3_out;

  not not_1 (not_1_out, Opcode_1);
  not not_2 (not_2_out, Opcode_0);
  and and_1 (PC_Change_0, Opcode_3, Opcode_2, not_3_out);
  not not_3 (not_3_out, Opcode_0);
  and and_2 (and_2_out, Opcode_3, Opcode_2, not_1_out, Opcode_0);
  or or_1 (PC_Change_1, and_2_out, and_3_out);
  and and_3 (and_3_out, Opcode_3, Opcode_2, Opcode_1, not_2_out);
endmodule
